// Logisim project finalproj (3).circ as structural Verilog: 7 circuits, main circuit main
module main (
  input  in_1,
  input  in_2,
  input  in_3,
  input  in_4,
  input  in_5,
  input  in_6,
  input  in_7,
  input  in_8,
  input  in_9,
  input  DataInput1,
  input  DataInput2,
  input  DataInput3,
  input  DataInput4,
  input  in_14
);

  wire alu_1_aout2, alu_1_aout3, alu_1_aout4, alu_2_aout3, alu_2_aout4, aluoutput0, aluoutput1, aluoutput2,
       aluoutput3, and_1_out, and_2_out, and_3_out, and_4_out, and_5_out, and_6_out, and_7_out, and_8_out,
       and_9_out, and_10_out, and_11_out, and_12_out, and_13_out, and_14_out, and_15_out, and_16_out,
       and_17_out, and_18_out, and_19_out, and_20_out, and_21_out, and_22_out, and_23_out, and_24_out,
       and_25_out, and_26_out, and_27_out, and_28_out, and_29_out, and_30_out, and_31_out, and_32_out,
       and_33_out, and_34_out, and_35_out, and_36_out, and_37_out, and_38_out, and_39_out, and_40_out,
       and_41_out, and_42_out, and_43_out, and_44_out, and_45_out, and_46_out, and_47_out, and_48_out,
       and_49_out, and_50_out, and_51_out, and_52_out, and_53_out, and_54_out, and_55_out, and_56_out,
       and_57_out, and_58_out, and_59_out, and_60_out, and_61_out, and_62_out, and_63_out, and_64_out,
       and_65_out, and_66_out, and_67_out, and_68_out, and_69_out, and_70_out, and_71_out, and_72_out,
       and_73_out, and_74_out, and_75_out, and_76_out, and_77_out, and_78_out, and_79_out, and_80_out,
       and_81_out, and_90_out, and_91_out, and_92_out, and_93_out, and_94_out, and_95_out, and_96_out,
       and_97_out, and_99_out, and_100_out, and_101_out, and_102_out, and_103_out, and_104_out, and_105_out,
       and_106_out, and_107_out, and_108_out, and_109_out, and_110_out, and_111_out, and_112_out,
       and_113_out, and_114_out, and_115_out, and_116_out, and_117_out, and_118_out, and_119_out,
       and_120_out, and_121_out, and_122_out, and_123_out, and_124_out, and_125_out, and_126_out,
       and_127_out, and_128_out, and_129_out, and_130_out, and_131_out, and_132_out, and_133_out,
       and_134_out, and_135_out, and_136_out, and_137_out, and_138_out, and_139_out, and_140_out,
       and_141_out, and_142_out, and_143_out, and_144_out, and_145_out, and_146_out, and_147_out,
       and_148_out, and_149_out, and_150_out, and_151_out, and_152_out, and_153_out, and_154_out,
       and_155_out, and_156_out, and_157_out, and_158_out, and_159_out, and_160_out, and_161_out,
       and_162_out, and_163_out, and_164_out, and_165_out, and_166_out, and_167_out, and_168_out,
       and_169_out, and_170_out, and_171_out, and_172_out, and_173_out, and_174_out, and_175_out,
       and_176_out, and_177_out, clk, clock_1_out, d_ff_1_q, d_ff_2_q, d_ff_3_q, d_ff_4_q, d_ff_5_q,
       d_ff_6_q, d_ff_7_q, d_ff_8_q, d_ff_9_q, d_ff_10_q, d_ff_11_q, d_ff_12_q, d_ff_13_q, d_ff_14_q,
       d_ff_15_q, d_ff_16_q, d_ff_17_q, d_ff_18_q, d_ff_19_q, d_ff_20_q, d_ff_21_q, d_ff_22_q, d_ff_23_q,
       d_ff_24_q, d_ff_25_q, d_ff_26_q, d_ff_27_q, d_ff_28_q, d_ff_29_q, d_ff_30_q, d_ff_32_q, d_ff_33_q,
       d_ff_34_q, d_ff_35_q, d_ff_36_q, d_ff_37_q, d_ff_38_q, d_ff_39_q, d_ff_40_q, d_ff_41_q, d_ff_42_q,
       d_ff_43_q, d_ff_44_q, d_ff_45_q, d_ff_46_q, d_ff_47_q, d_ff_49_q, d_ff_50_q, d_ff_51_q, d_ff_52_q,
       d_ff_54_q, d_ff_55_q, d_ff_56_q, d_ff_57_q, d_ff_58_q, d_ff_59_q, d_ff_61_q, d_ff_62_q, d_ff_63_q,
       d_ff_65_q, d_ff_68_q, d_ff_69_q, d_ff_70_q, d_ff_71_q, d_ff_72_q, d_ff_73_q, d_ff_74_q, d_ff_75_q,
       d_ff_76_q, d_ff_77_q, d_ff_78_q, d_ff_79_q, d_ff_80_q, d_ff_81_q, d_ff_82_q, d_ff_83_q, d_ff_84_q,
       d_ff_85_q, d_ff_87_q, d_ff_89_q, d_ff_90_q, d_ff_91_q, d_ff_94_q, d_ff_95_q, d_ff_96_q, d_ff_97_q,
       dataaddress, datamode, datarainput0, datarainput1, datarainput2, datarainput3, dataramoutput0,
       dataramoutput1, dataramoutput2, dataramoutput3, halt, Halt_out, load, loadinput0, loadinput1,
       loadinput2, loadinput3, not_1_out, not_2_out, not_3_out, not_4_out, not_5_out, not_6_out, not_7_out,
       not_8_out, not_9_out, not_10_out, not_11_out, not_12_out, not_13_out, not_14_out, not_15_out,
       not_16_out, not_17_out, not_18_out, not_20_out, not_23_out, not_24_out, not_25_out, not_26_out,
       not_27_out, not_28_out, not_29_out, not_30_out, not_31_out, not_32_out, not_33_out, not_34_out,
       not_35_out, not_36_out, not_37_out, not_38_out, not_39_out, not_40_out, not_41_out, not_42_out,
       or_1_out, or_2_out, or_3_out, or_4_out, or_5_out, or_6_out, or_7_out, or_9_out, or_10_out, or_11_out,
       or_14_out, or_15_out, or_16_out, or_17_out, or_18_out, or_19_out, or_20_out, or_21_out, or_22_out,
       or_23_out, or_24_out, or_25_out, or_26_out, register1or2, registermode, registermodeload,
       registeroutput0, registeroutput1, registeroutput2, registeroutput3, save;
  wire [1:0] counter;

  ALU alu_1 (
    .L2(d_ff_1_q), .L3(d_ff_2_q), .L4(d_ff_3_q), .R1(in_9), .R2(in_8), .R3(in_7), .R4(in_6), .cmd(in_5),
    .AOUT2(alu_1_aout2), .AOUT3(alu_1_aout3), .AOUT4(alu_1_aout4));  // open: L1, Zero, Negative, Overflow, AOUT1
  D_Flip_Flop #(.trigger("falling")) d_ff_1 (.D(alu_1_aout2), .clk(clk), .Q(d_ff_1_q));  // open: Qn, preset, reset
  D_Flip_Flop #(.trigger("falling")) d_ff_2 (.D(alu_1_aout3), .clk(clk), .Q(d_ff_2_q));  // open: Qn, preset, reset
  D_Flip_Flop #(.trigger("falling")) d_ff_3 (.D(alu_1_aout4), .clk(clk), .Q(d_ff_3_q));  // open: Qn, preset, reset
  D_Flip_Flop #(.trigger("falling")) d_ff_4 (.D(d_ff_1_q), .clk(clk), .Q(d_ff_4_q));  // open: Qn, preset, reset
  D_Flip_Flop #(.trigger("falling")) d_ff_5 (.D(d_ff_2_q), .clk(clk), .Q(d_ff_5_q));  // open: Qn, preset, reset
  not not_1 (not_1_out, d_ff_6_q);
  not not_2 (not_2_out, d_ff_5_q);
  not not_3 (not_3_out, d_ff_5_q);
  not not_4 (not_4_out, d_ff_6_q);
  not not_5 (not_5_out, d_ff_4_q);
  not not_6 (not_6_out, d_ff_4_q);
  not not_7 (not_7_out, d_ff_6_q);
  not not_8 (not_8_out, d_ff_4_q);
  not not_9 (not_9_out, d_ff_5_q);
  not not_10 (not_10_out, d_ff_4_q);
  not not_11 (not_11_out, d_ff_5_q);
  not not_12 (not_12_out, d_ff_6_q);
  D_Flip_Flop #(.trigger("falling")) d_ff_6 (.D(d_ff_3_q), .clk(clk), .Q(d_ff_6_q));  // open: Qn, preset, reset
  and and_1 (and_1_out, d_ff_4_q, d_ff_5_q, clk, d_ff_6_q);
  and and_2 (and_2_out, and_1_out, not_13_out);
  and and_3 (and_3_out, d_ff_4_q, d_ff_5_q, clk, not_1_out);
  and and_4 (and_4_out, and_3_out, not_13_out);
  and and_5 (and_5_out, d_ff_4_q, not_2_out, clk, d_ff_6_q);
  and and_6 (and_6_out, and_5_out, not_13_out);
  and and_7 (and_7_out, d_ff_4_q, not_3_out, clk, not_4_out);
  and and_8 (and_8_out, and_7_out, not_13_out);
  and and_9 (and_9_out, not_5_out, d_ff_5_q, clk, d_ff_6_q);
  and and_10 (and_10_out, and_9_out, not_13_out);
  and and_11 (and_11_out, not_6_out, d_ff_5_q, clk, not_7_out);
  and and_12 (and_12_out, and_11_out, not_13_out);
  and and_13 (and_13_out, not_8_out, not_9_out, clk, d_ff_6_q);
  and and_14 (and_14_out, and_13_out, not_13_out);
  and and_15 (and_15_out, not_10_out, not_11_out, clk, not_12_out);
  and and_16 (and_16_out, and_15_out, not_13_out);
  D_Flip_Flop #(.trigger("falling")) d_ff_7 (.D(in_14), .clk(clk), .Q(d_ff_7_q));  // open: Qn, preset, reset
  not not_13 (not_13_out, d_ff_7_q);
  and and_17 (and_17_out, and_1_out, not_13_out, d_ff_16_q);
  D_Flip_Flop #(.trigger("high")) d_ff_8 (.D(and_17_out), .clk(and_2_out), .Q(d_ff_8_q));  // open: Qn, preset, reset
  and and_18 (and_18_out, and_3_out, not_13_out, d_ff_16_q);
  D_Flip_Flop #(.trigger("high")) d_ff_9 (.D(and_18_out), .clk(and_4_out), .Q(d_ff_9_q));  // open: Qn, preset, reset
  and and_19 (and_19_out, and_5_out, not_13_out, d_ff_16_q);
  D_Flip_Flop #(.trigger("high")) d_ff_10 (.D(and_19_out), .clk(and_6_out), .Q(d_ff_10_q));  // open: Qn, preset, reset
  and and_20 (and_20_out, and_7_out, not_13_out, d_ff_16_q);
  D_Flip_Flop #(.trigger("high")) d_ff_11 (.D(and_20_out), .clk(and_8_out), .Q(d_ff_11_q));  // open: Qn, preset, reset
  and and_21 (and_21_out, and_9_out, not_13_out, d_ff_16_q);
  D_Flip_Flop #(.trigger("high")) d_ff_12 (.D(and_21_out), .clk(and_10_out), .Q(d_ff_12_q));  // open: Qn, preset, reset
  and and_22 (and_22_out, and_11_out, not_13_out, d_ff_16_q);
  D_Flip_Flop #(.trigger("high")) d_ff_13 (.D(and_22_out), .clk(and_12_out), .Q(d_ff_13_q));  // open: Qn, preset, reset
  and and_23 (and_23_out, and_13_out, not_13_out, d_ff_16_q);
  D_Flip_Flop #(.trigger("high")) d_ff_14 (.D(and_23_out), .clk(and_14_out), .Q(d_ff_14_q));  // open: Qn, preset, reset
  and and_24 (and_24_out, and_15_out, not_13_out, d_ff_16_q);
  D_Flip_Flop #(.trigger("high")) d_ff_15 (.D(and_24_out), .clk(and_16_out), .Q(d_ff_15_q));  // open: Qn, preset, reset
  or or_1 (or_1_out, and_25_out, and_26_out, and_27_out, and_28_out, and_29_out, and_30_out, and_31_out, and_32_out);
  and and_25 (and_25_out, d_ff_8_q, and_1_out, d_ff_7_q);
  and and_26 (and_26_out, d_ff_9_q, and_3_out, d_ff_7_q);
  and and_27 (and_27_out, d_ff_10_q, and_5_out, d_ff_7_q);
  and and_28 (and_28_out, d_ff_11_q, and_7_out, d_ff_7_q);
  and and_29 (and_29_out, d_ff_12_q, and_9_out, d_ff_7_q);
  and and_30 (and_30_out, d_ff_13_q, and_11_out, d_ff_7_q);
  and and_31 (and_31_out, d_ff_14_q, and_13_out, d_ff_7_q);
  and and_32 (and_32_out, d_ff_15_q, and_15_out, d_ff_7_q);
  D_Flip_Flop #(.trigger("falling")) d_ff_16 (.D(DataInput1), .clk(clk), .Q(d_ff_16_q));  // open: Qn, preset, reset
  D_Flip_Flop #(.trigger("falling")) d_ff_17 (.D(DataInput2), .clk(clk), .Q(d_ff_17_q));  // open: Qn, preset, reset
  and and_33 (and_33_out, and_1_out, not_13_out, d_ff_17_q);
  D_Flip_Flop #(.trigger("high")) d_ff_18 (.D(and_33_out), .clk(and_2_out), .Q(d_ff_18_q));  // open: Qn, preset, reset
  and and_34 (and_34_out, and_3_out, not_13_out, d_ff_17_q);
  D_Flip_Flop #(.trigger("high")) d_ff_19 (.D(and_34_out), .clk(and_4_out), .Q(d_ff_19_q));  // open: Qn, preset, reset
  and and_35 (and_35_out, and_5_out, not_13_out, d_ff_17_q);
  D_Flip_Flop #(.trigger("high")) d_ff_20 (.D(and_35_out), .clk(and_6_out), .Q(d_ff_20_q));  // open: Qn, preset, reset
  and and_36 (and_36_out, and_7_out, not_13_out, d_ff_17_q);
  D_Flip_Flop #(.trigger("high")) d_ff_21 (.D(and_36_out), .clk(and_8_out), .Q(d_ff_21_q));  // open: Qn, preset, reset
  and and_37 (and_37_out, and_9_out, not_13_out, d_ff_17_q);
  D_Flip_Flop #(.trigger("high")) d_ff_22 (.D(and_37_out), .clk(and_10_out), .Q(d_ff_22_q));  // open: Qn, preset, reset
  and and_38 (and_38_out, and_11_out, not_13_out, d_ff_17_q);
  D_Flip_Flop #(.trigger("high")) d_ff_23 (.D(and_38_out), .clk(and_12_out), .Q(d_ff_23_q));  // open: Qn, preset, reset
  and and_39 (and_39_out, and_13_out, not_13_out, d_ff_17_q);
  D_Flip_Flop #(.trigger("high")) d_ff_24 (.D(and_39_out), .clk(and_14_out), .Q(d_ff_24_q));  // open: Qn, preset, reset
  and and_40 (and_40_out, and_15_out, not_13_out, d_ff_17_q);
  D_Flip_Flop #(.trigger("high")) d_ff_25 (.D(and_40_out), .clk(and_16_out), .Q(d_ff_25_q));  // open: Qn, preset, reset
  D_Flip_Flop #(.trigger("falling")) d_ff_26 (.D(DataInput3), .clk(clk), .Q(d_ff_26_q));  // open: Qn, preset, reset
  D_Flip_Flop #(.trigger("high")) d_ff_27 (.D(or_1_out), .clk(clk), .Q(d_ff_27_q));  // open: Qn, preset, reset
  or or_2 (or_2_out, and_41_out, and_42_out, and_43_out, and_44_out, and_45_out, and_46_out, and_47_out, and_48_out);
  and and_41 (and_41_out, d_ff_18_q, and_1_out, d_ff_7_q);
  and and_42 (and_42_out, d_ff_19_q, and_3_out, d_ff_7_q);
  and and_43 (and_43_out, d_ff_20_q, and_5_out, d_ff_7_q);
  and and_44 (and_44_out, d_ff_21_q, and_7_out, d_ff_7_q);
  and and_45 (and_45_out, d_ff_22_q, and_9_out, d_ff_7_q);
  and and_46 (and_46_out, d_ff_23_q, and_11_out, d_ff_7_q);
  and and_47 (and_47_out, d_ff_24_q, and_13_out, d_ff_7_q);
  and and_48 (and_48_out, d_ff_25_q, and_15_out, d_ff_7_q);
  D_Flip_Flop #(.trigger("falling")) d_ff_28 (.D(DataInput4), .clk(clk), .Q(d_ff_28_q));  // open: Qn, preset, reset
  D_Flip_Flop #(.trigger("high")) d_ff_29 (.D(or_2_out), .clk(clk), .Q(d_ff_29_q));  // open: Qn, preset, reset
  D_Flip_Flop #(.trigger("high")) d_ff_30 (.D(or_3_out), .clk(clk), .Q(d_ff_30_q));  // open: Qn, preset, reset
  and and_49 (and_49_out, and_1_out, not_13_out, d_ff_26_q);
  and and_50 (and_50_out, and_3_out, not_13_out, d_ff_26_q);
  and and_51 (and_51_out, and_5_out, not_13_out, d_ff_26_q);
  and and_52 (and_52_out, and_7_out, not_13_out, d_ff_26_q);
  and and_53 (and_53_out, and_9_out, not_13_out, d_ff_26_q);
  and and_54 (and_54_out, and_11_out, not_13_out, d_ff_26_q);
  and and_55 (and_55_out, and_13_out, not_13_out, d_ff_26_q);
  and and_56 (and_56_out, and_15_out, not_13_out, d_ff_26_q);
  D_Flip_Flop #(.trigger("high")) d_ff_31 (.D(or_4_out), .clk(clk), .Q(dataaddress));  // open: Qn, preset, reset
  D_Flip_Flop #(.trigger("high")) d_ff_32 (.D(and_49_out), .clk(and_2_out), .Q(d_ff_32_q));  // open: Qn, preset, reset
  D_Flip_Flop #(.trigger("high")) d_ff_33 (.D(and_50_out), .clk(and_4_out), .Q(d_ff_33_q));  // open: Qn, preset, reset
  D_Flip_Flop #(.trigger("high")) d_ff_34 (.D(and_51_out), .clk(and_6_out), .Q(d_ff_34_q));  // open: Qn, preset, reset
  D_Flip_Flop #(.trigger("high")) d_ff_35 (.D(and_52_out), .clk(and_8_out), .Q(d_ff_35_q));  // open: Qn, preset, reset
  D_Flip_Flop #(.trigger("high")) d_ff_36 (.D(and_53_out), .clk(and_10_out), .Q(d_ff_36_q));  // open: Qn, preset, reset
  D_Flip_Flop #(.trigger("high")) d_ff_37 (.D(and_54_out), .clk(and_12_out), .Q(d_ff_37_q));  // open: Qn, preset, reset
  D_Flip_Flop #(.trigger("high")) d_ff_38 (.D(and_55_out), .clk(and_14_out), .Q(d_ff_38_q));  // open: Qn, preset, reset
  D_Flip_Flop #(.trigger("high")) d_ff_39 (.D(and_56_out), .clk(and_16_out), .Q(d_ff_39_q));  // open: Qn, preset, reset
  or or_3 (or_3_out, and_57_out, and_58_out, and_59_out, and_60_out, and_61_out, and_62_out, and_63_out, and_64_out);
  and and_57 (and_57_out, d_ff_32_q, and_1_out, d_ff_7_q);
  and and_58 (and_58_out, d_ff_33_q, and_3_out, d_ff_7_q);
  and and_59 (and_59_out, d_ff_34_q, and_5_out, d_ff_7_q);
  and and_60 (and_60_out, d_ff_35_q, and_7_out, d_ff_7_q);
  and and_61 (and_61_out, d_ff_36_q, and_9_out, d_ff_7_q);
  and and_62 (and_62_out, d_ff_37_q, and_11_out, d_ff_7_q);
  and and_63 (and_63_out, d_ff_38_q, and_13_out, d_ff_7_q);
  and and_64 (and_64_out, d_ff_39_q, and_15_out, d_ff_7_q);
  and and_65 (and_65_out, and_1_out, not_13_out, d_ff_28_q);
  D_Flip_Flop #(.trigger("high")) d_ff_40 (.D(and_65_out), .clk(and_2_out), .Q(d_ff_40_q));  // open: Qn, preset, reset
  and and_66 (and_66_out, and_3_out, not_13_out, d_ff_28_q);
  D_Flip_Flop #(.trigger("high")) d_ff_41 (.D(and_66_out), .clk(and_4_out), .Q(d_ff_41_q));  // open: Qn, preset, reset
  and and_67 (and_67_out, and_5_out, not_13_out, d_ff_28_q);
  D_Flip_Flop #(.trigger("high")) d_ff_42 (.D(and_67_out), .clk(and_6_out), .Q(d_ff_42_q));  // open: Qn, preset, reset
  and and_68 (and_68_out, and_7_out, not_13_out, d_ff_28_q);
  D_Flip_Flop #(.trigger("high")) d_ff_43 (.D(and_68_out), .clk(and_8_out), .Q(d_ff_43_q));  // open: Qn, preset, reset
  and and_69 (and_69_out, and_9_out, not_13_out, d_ff_28_q);
  D_Flip_Flop #(.trigger("high")) d_ff_44 (.D(and_69_out), .clk(and_10_out), .Q(d_ff_44_q));  // open: Qn, preset, reset
  and and_70 (and_70_out, and_11_out, not_13_out, d_ff_28_q);
  D_Flip_Flop #(.trigger("high")) d_ff_45 (.D(and_70_out), .clk(and_12_out), .Q(d_ff_45_q));  // open: Qn, preset, reset
  and and_71 (and_71_out, and_13_out, not_13_out, d_ff_28_q);
  D_Flip_Flop #(.trigger("high")) d_ff_46 (.D(and_71_out), .clk(and_14_out), .Q(d_ff_46_q));  // open: Qn, preset, reset
  and and_72 (and_72_out, and_15_out, not_13_out, d_ff_28_q);
  D_Flip_Flop #(.trigger("high")) d_ff_47 (.D(and_72_out), .clk(and_16_out), .Q(d_ff_47_q));  // open: Qn, preset, reset
  or or_4 (or_4_out, and_73_out, and_74_out, and_75_out, and_76_out, and_77_out, and_78_out, and_79_out, and_80_out);
  and and_73 (and_73_out, d_ff_40_q, and_1_out, d_ff_7_q);
  and and_74 (and_74_out, d_ff_41_q, and_3_out, d_ff_7_q);
  and and_75 (and_75_out, d_ff_42_q, and_5_out, d_ff_7_q);
  and and_76 (and_76_out, d_ff_43_q, and_7_out, d_ff_7_q);
  and and_77 (and_77_out, d_ff_44_q, and_9_out, d_ff_7_q);
  and and_78 (and_78_out, d_ff_45_q, and_11_out, d_ff_7_q);
  and and_79 (and_79_out, d_ff_46_q, and_13_out, d_ff_7_q);
  and and_80 (and_80_out, d_ff_47_q, and_15_out, d_ff_7_q);
  and and_81 (and_81_out, dataaddress, in_1);
  not not_14 (not_14_out, d_ff_49_q);
  not not_15 (not_15_out, d_ff_50_q);
  not not_16 (not_16_out, d_ff_49_q);
  not not_17 (not_17_out, d_ff_50_q);
  not not_18 (not_18_out, and_81_out);
  and and_82 (loadinput0, dataramoutput0, load);
  and and_83 (loadinput1, dataramoutput1, load);
  and and_84 (loadinput2, dataramoutput2, load);
  and and_85 (loadinput3, dataramoutput3, load);
  and u_Load (load, not_14_out, not_15_out);
  and u_Save (save, not_16_out, d_ff_50_q);
  // AND_Gate Add has open pins: in0=d_ff_49_q, in1=not_17_out, out=open
  // AND_Gate Sub has open pins: in0=d_ff_49_q, in1=not_18_out, in2=d_ff_50_q, out=open
  and u_Halt (Halt_out, d_ff_49_q, and_81_out, d_ff_50_q);
  not not_19 (halt, Halt_out);
  D_Flip_Flop d_ff_48 (.D(alu_2_aout3), .clk(not_20_out), .Q(counter[1]));  // open: Qn, preset, reset
  not not_20 (not_20_out, clk);
  not not_21 (registermodeload, load);
  not not_22 (datamode, save);
  D_Flip_Flop d_ff_49 (.D(d_ff_27_q), .clk(clk), .Q(d_ff_49_q));  // open: Qn, preset, reset
  D_Flip_Flop d_ff_50 (.D(d_ff_29_q), .clk(clk), .Q(d_ff_50_q));  // open: Qn, preset, reset
  D_Flip_Flop d_ff_51 (.D(in_1), .clk(clk), .Q(d_ff_51_q));  // open: Qn, preset, reset
  D_Flip_Flop d_ff_52 (.D(dataaddress), .clk(clk), .Q(d_ff_52_q));  // open: Qn, preset, reset
  D_Flip_Flop d_ff_53 (.D(alu_2_aout4), .clk(not_20_out), .Q(counter[0]));  // open: Qn, preset, reset
  not not_23 (not_23_out, counter[1]);
  not not_24 (not_24_out, counter[0]);
  not not_25 (not_25_out, counter[1]);
  not not_26 (not_26_out, counter[0]);
  not not_27 (not_27_out, counter[1]);
  not not_28 (not_28_out, counter[0]);
  not not_29 (not_29_out, counter[1]);
  not not_30 (not_30_out, counter[0]);
  and and_86 (datarainput0, registeroutput0, save);
  and and_87 (datarainput1, registeroutput1, save);
  and and_88 (datarainput2, registeroutput2, save);
  and and_89 (datarainput3, registeroutput3, save);
  ALU alu_2 (
    .L4(in_2), .R3(counter[1]), .R4(counter[0]), .AOUT3(alu_2_aout3), .AOUT4(alu_2_aout4));  // open: L1, L2, L3, R1, R2, cmd, Zero, Negative, Overflow, AOUT1, AOUT2
  and and_90 (and_90_out, not_23_out, in_3, not_24_out);
  and and_91 (and_91_out, not_25_out, in_3, counter[0]);
  and and_92 (and_92_out, counter[1], in_3, not_26_out);
  and and_93 (and_93_out, counter[1], in_3, counter[0]);
  not not_31 (not_31_out, and_93_out);
  and and_94 (and_94_out, not_27_out, in_4, not_28_out);
  and and_95 (and_95_out, not_29_out, in_4, counter[0]);
  and and_96 (and_96_out, counter[1], in_4, not_30_out);
  and and_97 (and_97_out, counter[1], in_4, counter[0]);
  or or_5 (or_5_out, and_90_out, and_94_out);
  Clock clock_1 (.out(clock_1_out));
  or or_6 (or_6_out, and_91_out, and_95_out);
  not not_32 (not_32_out, and_92_out);
  and and_98 (clk, clock_1_out, halt);
  or or_7 (or_7_out, not_32_out, and_96_out);
  // OR_Gate or_8 has open pins: in0=not_31_out, in1=and_97_out, out=open
  and and_99 (and_99_out, or_7_out, d_ff_51_q);
  and and_100 (and_100_out, d_ff_51_q, or_5_out);
  and and_101 (and_101_out, d_ff_52_q, or_6_out);
  or or_9 (or_9_out, or_5_out, or_6_out);
  or or_10 (or_10_out, and_99_out, and_100_out, and_101_out);
  or or_11 (or_11_out, load, save);
  or or_12 (registermode, and_102_out, and_103_out);
  and and_102 (and_102_out, registermodeload, or_11_out);
  and and_103 (and_103_out, not_33_out, or_9_out);
  not not_33 (not_33_out, or_11_out);
  or or_13 (register1or2, and_104_out, and_105_out);
  and and_104 (and_104_out, in_1, or_11_out);
  and and_105 (and_105_out, not_34_out, or_10_out);
  not not_34 (not_34_out, or_11_out);
  not not_35 (not_35_out, d_ff_54_q);
  D_Flip_Flop #(.trigger("falling")) d_ff_54 (.D(register1or2), .clk(clk), .Q(d_ff_54_q));  // open: Qn, preset, reset
  and and_106 (and_106_out, clk, d_ff_54_q);
  and and_107 (and_107_out, clk, not_35_out);
  and and_108 (and_108_out, and_106_out, not_36_out);
  and and_109 (and_109_out, and_107_out, not_36_out);
  not not_36 (not_36_out, d_ff_55_q);
  D_Flip_Flop #(.trigger("falling")) d_ff_55 (.D(registermode), .clk(clk), .Q(d_ff_55_q));  // open: Qn, preset, reset
  and and_110 (and_110_out, and_106_out, not_36_out, d_ff_58_q);
  D_Flip_Flop #(.trigger("high")) d_ff_56 (
    .D(and_110_out), .clk(and_108_out), .Q(d_ff_56_q));  // open: Qn, preset, reset
  and and_111 (and_111_out, and_107_out, not_36_out, d_ff_58_q);
  D_Flip_Flop #(.trigger("high")) d_ff_57 (
    .D(and_111_out), .clk(and_109_out), .Q(d_ff_57_q));  // open: Qn, preset, reset
  or or_14 (or_14_out, load, save);
  or or_15 (or_15_out, and_112_out, and_113_out);
  and and_112 (and_112_out, d_ff_56_q, and_106_out, d_ff_55_q);
  and and_113 (and_113_out, d_ff_57_q, and_107_out, d_ff_55_q);
  D_Flip_Flop #(.trigger("falling")) d_ff_58 (.D(or_16_out), .clk(clk), .Q(d_ff_58_q));  // open: Qn, preset, reset
  or or_16 (or_16_out, and_114_out, and_115_out);
  and and_114 (and_114_out, aluoutput3, not_37_out);
  and and_115 (and_115_out, or_14_out, loadinput3);
  not not_37 (not_37_out, or_14_out);
  D_Flip_Flop #(.trigger("falling")) d_ff_59 (.D(or_17_out), .clk(clk), .Q(d_ff_59_q));  // open: Qn, preset, reset
  or or_17 (or_17_out, and_116_out, and_117_out);
  and and_116 (and_116_out, aluoutput2, not_38_out);
  and and_117 (and_117_out, or_14_out, loadinput2);
  not not_38 (not_38_out, or_14_out);
  D_Flip_Flop #(.trigger("high")) d_ff_60 (.D(or_15_out), .clk(clk), .Q(registeroutput3));  // open: Qn, preset, reset
  and and_118 (and_118_out, and_106_out, not_36_out, d_ff_59_q);
  D_Flip_Flop #(.trigger("high")) d_ff_61 (
    .D(and_118_out), .clk(and_108_out), .Q(d_ff_61_q));  // open: Qn, preset, reset
  and and_119 (and_119_out, and_107_out, not_36_out, d_ff_59_q);
  D_Flip_Flop #(.trigger("high")) d_ff_62 (
    .D(and_119_out), .clk(and_109_out), .Q(d_ff_62_q));  // open: Qn, preset, reset
  D_Flip_Flop #(.trigger("falling")) d_ff_63 (.D(or_18_out), .clk(clk), .Q(d_ff_63_q));  // open: Qn, preset, reset
  or or_18 (or_18_out, and_120_out, and_121_out);
  and and_120 (and_120_out, aluoutput1, not_39_out);
  and and_121 (and_121_out, or_14_out, loadinput1);
  not not_39 (not_39_out, or_14_out);
  D_Flip_Flop #(.trigger("high")) d_ff_64 (.D(or_19_out), .clk(clk), .Q(registeroutput2));  // open: Qn, preset, reset
  or or_19 (or_19_out, and_122_out, and_123_out);
  and and_122 (and_122_out, d_ff_61_q, and_106_out, d_ff_55_q);
  and and_123 (and_123_out, d_ff_62_q, and_107_out, d_ff_55_q);
  D_Flip_Flop #(.trigger("falling")) d_ff_65 (.D(or_20_out), .clk(clk), .Q(d_ff_65_q));  // open: Qn, preset, reset
  or or_20 (or_20_out, and_124_out, and_125_out);
  and and_124 (and_124_out, aluoutput0, not_40_out);
  and and_125 (and_125_out, or_14_out, loadinput0);
  not not_40 (not_40_out, or_14_out);
  D_Flip_Flop #(.trigger("high")) d_ff_66 (.D(or_21_out), .clk(clk), .Q(registeroutput1));  // open: Qn, preset, reset
  D_Flip_Flop #(.trigger("high")) d_ff_67 (.D(or_22_out), .clk(clk), .Q(registeroutput0));  // open: Qn, preset, reset
  or or_21 (or_21_out, and_128_out, and_129_out);
  and and_126 (and_126_out, and_106_out, not_36_out, d_ff_63_q);
  D_Flip_Flop #(.trigger("high")) d_ff_68 (
    .D(and_126_out), .clk(and_108_out), .Q(d_ff_68_q));  // open: Qn, preset, reset
  and and_127 (and_127_out, and_107_out, not_36_out, d_ff_63_q);
  D_Flip_Flop #(.trigger("high")) d_ff_69 (
    .D(and_127_out), .clk(and_109_out), .Q(d_ff_69_q));  // open: Qn, preset, reset
  and and_128 (and_128_out, d_ff_68_q, and_106_out, d_ff_55_q);
  and and_129 (and_129_out, d_ff_69_q, and_107_out, d_ff_55_q);
  or or_22 (or_22_out, and_132_out, and_133_out);
  and and_130 (and_130_out, and_106_out, not_36_out, d_ff_65_q);
  D_Flip_Flop #(.trigger("high")) d_ff_70 (
    .D(and_130_out), .clk(and_108_out), .Q(d_ff_70_q));  // open: Qn, preset, reset
  and and_131 (and_131_out, and_107_out, not_36_out, d_ff_65_q);
  D_Flip_Flop #(.trigger("high")) d_ff_71 (
    .D(and_131_out), .clk(and_109_out), .Q(d_ff_71_q));  // open: Qn, preset, reset
  and and_132 (and_132_out, d_ff_70_q, and_106_out, d_ff_55_q);
  and and_133 (and_133_out, d_ff_71_q, and_107_out, d_ff_55_q);
  and and_134 (and_134_out, registeroutput2, or_6_out);
  and and_135 (and_135_out, registeroutput3, or_5_out);
  and and_136 (and_136_out, registeroutput2, or_5_out);
  and and_137 (and_137_out, registeroutput1, or_5_out);
  and and_138 (and_138_out, registeroutput0, or_5_out);
  and and_139 (and_139_out, registeroutput3, or_6_out);
  D_Flip_Flop #(.trigger("high")) d_ff_72 (
    .D(and_139_out), .clk(and_140_out), .Q(d_ff_72_q));  // open: Qn, preset, reset
  and and_140 (and_140_out, or_6_out, clk);
  D_Flip_Flop #(.trigger("high")) d_ff_73 (
    .D(and_134_out), .clk(and_141_out), .Q(d_ff_73_q));  // open: Qn, preset, reset
  and and_141 (and_141_out, or_6_out, clk);
  and and_142 (and_142_out, registeroutput1, or_6_out);
  D_Flip_Flop #(.trigger("high")) d_ff_74 (
    .D(and_142_out), .clk(and_143_out), .Q(d_ff_74_q));  // open: Qn, preset, reset
  and and_143 (and_143_out, or_6_out, clk);
  and and_144 (and_144_out, registeroutput0, or_6_out);
  D_Flip_Flop #(.trigger("high")) d_ff_75 (
    .D(and_144_out), .clk(and_145_out), .Q(d_ff_75_q));  // open: Qn, preset, reset
  and and_145 (and_145_out, or_6_out, clk);
  D_Flip_Flop #(.trigger("high")) d_ff_76 (
    .D(and_135_out), .clk(and_146_out), .Q(d_ff_76_q));  // open: Qn, preset, reset
  and and_146 (and_146_out, or_5_out, clk);
  D_Flip_Flop #(.trigger("high")) d_ff_77 (
    .D(and_136_out), .clk(and_147_out), .Q(d_ff_77_q));  // open: Qn, preset, reset
  and and_147 (and_147_out, or_5_out, clk);
  D_Flip_Flop #(.trigger("high")) d_ff_78 (
    .D(and_137_out), .clk(and_148_out), .Q(d_ff_78_q));  // open: Qn, preset, reset
  and and_148 (and_148_out, or_5_out, clk);
  D_Flip_Flop #(.trigger("high")) d_ff_79 (
    .D(and_138_out), .clk(and_149_out), .Q(d_ff_79_q));  // open: Qn, preset, reset
  and and_149 (and_149_out, or_5_out, clk);
  and and_150 (and_150_out, d_ff_72_q, or_7_out);
  and and_151 (and_151_out, d_ff_73_q, or_7_out);
  and and_152 (and_152_out, d_ff_74_q, or_7_out);
  and and_153 (and_153_out, d_ff_75_q, or_7_out);
  and and_154 (and_154_out, d_ff_76_q, or_7_out);
  and and_155 (and_155_out, d_ff_77_q, or_7_out);
  and and_156 (and_156_out, d_ff_78_q, or_7_out);
  and and_157 (and_157_out, d_ff_79_q, or_7_out);
  ALU alu_3 (
    .L1(and_150_out), .L2(and_151_out), .L3(and_152_out), .L4(and_153_out), .R1(and_154_out),
    .R2(and_155_out), .R3(and_156_out), .R4(and_157_out), .cmd(or_7_out), .AOUT1(aluoutput3),
    .AOUT2(aluoutput2), .AOUT3(aluoutput1), .AOUT4(aluoutput0));  // open: Zero, Negative, Overflow
  not not_41 (not_41_out, d_ff_80_q);
  and and_158 (and_158_out, clk, d_ff_80_q);
  and and_159 (and_159_out, clk, not_41_out);
  D_Flip_Flop #(.trigger("falling")) d_ff_80 (.D(dataaddress), .clk(clk), .Q(d_ff_80_q));  // open: Qn, preset, reset
  and and_160 (and_160_out, and_158_out, not_42_out);
  and and_161 (and_161_out, and_159_out, not_42_out);
  not not_42 (not_42_out, d_ff_81_q);
  D_Flip_Flop #(.trigger("falling")) d_ff_81 (.D(datamode), .clk(clk), .Q(d_ff_81_q));  // open: Qn, preset, reset
  and and_162 (and_162_out, and_158_out, not_42_out, d_ff_84_q);
  D_Flip_Flop #(.trigger("high")) d_ff_82 (
    .D(and_162_out), .clk(and_160_out), .Q(d_ff_82_q));  // open: Qn, preset, reset
  and and_163 (and_163_out, and_159_out, not_42_out, d_ff_84_q);
  D_Flip_Flop #(.trigger("high")) d_ff_83 (
    .D(and_163_out), .clk(and_161_out), .Q(d_ff_83_q));  // open: Qn, preset, reset
  or or_23 (or_23_out, and_164_out, and_165_out);
  and and_164 (and_164_out, d_ff_82_q, and_158_out, d_ff_81_q);
  and and_165 (and_165_out, d_ff_83_q, and_159_out, d_ff_81_q);
  D_Flip_Flop #(.trigger("falling")) d_ff_84 (.D(datarainput3), .clk(clk), .Q(d_ff_84_q));  // open: Qn, preset, reset
  D_Flip_Flop #(.trigger("falling")) d_ff_85 (.D(datarainput2), .clk(clk), .Q(d_ff_85_q));  // open: Qn, preset, reset
  D_Flip_Flop #(.trigger("high")) d_ff_86 (.D(or_23_out), .clk(clk), .Q(dataramoutput3));  // open: Qn, preset, reset
  D_Flip_Flop #(.trigger("falling")) d_ff_87 (.D(datarainput1), .clk(clk), .Q(d_ff_87_q));  // open: Qn, preset, reset
  D_Flip_Flop #(.trigger("high")) d_ff_88 (.D(or_24_out), .clk(clk), .Q(dataramoutput2));  // open: Qn, preset, reset
  or or_24 (or_24_out, and_168_out, and_169_out);
  and and_166 (and_166_out, and_158_out, not_42_out, d_ff_85_q);
  D_Flip_Flop #(.trigger("high")) d_ff_89 (
    .D(and_166_out), .clk(and_160_out), .Q(d_ff_89_q));  // open: Qn, preset, reset
  and and_167 (and_167_out, and_159_out, not_42_out, d_ff_85_q);
  D_Flip_Flop #(.trigger("high")) d_ff_90 (
    .D(and_167_out), .clk(and_161_out), .Q(d_ff_90_q));  // open: Qn, preset, reset
  D_Flip_Flop #(.trigger("falling")) d_ff_91 (.D(datarainput0), .clk(clk), .Q(d_ff_91_q));  // open: Qn, preset, reset
  D_Flip_Flop #(.trigger("high")) d_ff_92 (.D(or_25_out), .clk(clk), .Q(dataramoutput1));  // open: Qn, preset, reset
  and and_168 (and_168_out, d_ff_89_q, and_158_out, d_ff_81_q);
  and and_169 (and_169_out, d_ff_90_q, and_159_out, d_ff_81_q);
  D_Flip_Flop #(.trigger("high")) d_ff_93 (.D(or_26_out), .clk(clk), .Q(dataramoutput0));  // open: Qn, preset, reset
  or or_25 (or_25_out, and_172_out, and_173_out);
  and and_170 (and_170_out, and_158_out, not_42_out, d_ff_87_q);
  D_Flip_Flop #(.trigger("high")) d_ff_94 (
    .D(and_170_out), .clk(and_160_out), .Q(d_ff_94_q));  // open: Qn, preset, reset
  and and_171 (and_171_out, and_159_out, not_42_out, d_ff_87_q);
  D_Flip_Flop #(.trigger("high")) d_ff_95 (
    .D(and_171_out), .clk(and_161_out), .Q(d_ff_95_q));  // open: Qn, preset, reset
  and and_172 (and_172_out, d_ff_94_q, and_158_out, d_ff_81_q);
  and and_173 (and_173_out, d_ff_95_q, and_159_out, d_ff_81_q);
  and and_174 (and_174_out, and_158_out, not_42_out, d_ff_91_q);
  and and_175 (and_175_out, and_159_out, not_42_out, d_ff_91_q);
  or or_26 (or_26_out, and_176_out, and_177_out);
  and and_176 (and_176_out, d_ff_96_q, and_158_out, d_ff_81_q);
  D_Flip_Flop #(.trigger("high")) d_ff_96 (
    .D(and_174_out), .clk(and_160_out), .Q(d_ff_96_q));  // open: Qn, preset, reset
  and and_177 (and_177_out, d_ff_97_q, and_159_out, d_ff_81_q);
  D_Flip_Flop #(.trigger("high")) d_ff_97 (
    .D(and_175_out), .clk(and_161_out), .Q(d_ff_97_q));  // open: Qn, preset, reset

  // Other names for the same wires on the sheet: IR4 = dataaddress; IR3 = in_1; registeraddressload = in_1

  // Notes on the sheet:
  //   Leticia Huang 261068858
  //   Leticia Huang 261068858
  //   PC address
  //   PC
  //   Set 1 to Read from I-RAM
  //   4 pins always +1
  //   Top pin always 0 for cmd
  //   3-bit address input pins
  //   Mode input pin
  //   4-bit data input pins
  //   Instruction RAM
  //   IR
  //   PC plus4
  //   R1
  //   R0
  //   MULTIPLEXOR 
  //   REGISTER BLOCK
  //   MULTIPLEXOR
  //   DATA RAM
  //   ADDRESS 1
  //   ADDRESS 0
endmodule

module ALU (
  input  L1,
  input  L2,
  input  L3,
  input  L4,
  input  R1,
  input  R2,
  input  R3,
  input  R4,
  input  cmd,
  output Zero,
  output Negative,
  output Overflow,
  output AOUT1,
  output AOUT2,
  output AOUT3,
  output AOUT4
);

  wire and_1_out, and_2_out, and_3_out, and_4_out, and_5_out, and_6_out, and_7_out, and_8_out, and_9_out,
       and_10_out, and_11_out, and_12_out, and_13_out, and_14_out, and_15_out, and_16_out, and_17_out,
       and_18_out, and_19_out, and_20_out, and_21_out, and_22_out, and_24_out, and_25_out, and_26_out,
       and_27_out, Clock, fulladder_1_c, fulladder_2_c, fulladder_3_c, Neg_out, not_1_out, not_2_out,
       not_3_out, not_4_out, not_5_out, not_6_out, not_7_out, not_8_out, not_9_out, not_10_out, not_11_out,
       not_12_out, not_13_out, not_14_out, not_15_out, or_1_out, or_2_out, or_3_out, or_4_out, or_5_out,
       Pos_out, xor_2_out, xor_3_out, xor_4_out, xor_5_out;

  Clock clock_1 (.out(Clock));
  not not_1 (not_1_out, cmd);
  and and_1 (and_1_out, L1, Clock);
  and and_2 (and_2_out, L2, Clock);
  and and_3 (and_3_out, L3, Clock);
  fullAdder fulladder_1 (.A(or_1_out), .B(and_1_out), .Carry(fulladder_2_c), .C(fulladder_1_c), .Sum(AOUT1));
  and and_4 (and_4_out, L4, Clock);
  fullAdder fulladder_2 (.A(or_2_out), .B(and_2_out), .Carry(fulladder_3_c), .C(fulladder_2_c), .Sum(AOUT2));
  or or_1 (or_1_out, xor_2_out, and_6_out);
  fullAdder fulladder_3 (.A(or_3_out), .B(and_3_out), .Carry(and_5_out), .C(fulladder_3_c), .Sum(AOUT3));
  or or_2 (or_2_out, xor_3_out, and_8_out);
  or or_3 (or_3_out, xor_4_out, and_9_out);
  and and_5 (and_5_out, and_4_out, or_4_out);
  xor xor_1 (AOUT4, and_4_out, or_4_out);
  and and_6 (and_6_out, and_12_out, not_1_out);
  and and_7 (and_7_out, not_6_out, and_10_out);
  or or_4 (or_4_out, xor_5_out, and_14_out);
  not not_2 (not_2_out, AOUT4);
  not not_3 (not_3_out, AOUT3);
  not not_4 (not_4_out, AOUT2);
  not not_5 (not_5_out, AOUT1);
  and and_8 (and_8_out, and_13_out, not_1_out);
  and and_9 (and_9_out, and_17_out, not_1_out);
  xor xor_2 (xor_2_out, not_6_out, and_10_out);
  and and_10 (and_10_out, not_10_out, and_16_out);
  and and_11 (and_11_out, not_2_out, not_3_out, not_4_out, not_5_out);
  and and_12 (and_12_out, R1, Clock);
  and and_13 (and_13_out, R2, Clock);
  and and_14 (and_14_out, and_18_out, not_1_out);
  and and_15 (and_15_out, and_12_out, cmd);
  not not_6 (not_6_out, and_15_out);
  xor xor_3 (xor_3_out, not_10_out, and_16_out);
  and and_16 (and_16_out, not_11_out, and_22_out);
  not not_7 (not_7_out, or_1_out);
  not not_8 (not_8_out, and_1_out);
  not not_9 (not_9_out, or_1_out);
  and and_17 (and_17_out, R3, Clock);
  and and_18 (and_18_out, R4, Clock);
  and and_19 (and_19_out, and_13_out, cmd);
  and and_20 (and_20_out, and_17_out, cmd);
  and and_21 (and_21_out, and_18_out, cmd);
  not not_10 (not_10_out, and_19_out);
  not not_11 (not_11_out, and_20_out);
  not not_12 (not_12_out, and_21_out);
  xor xor_4 (xor_4_out, not_11_out, and_22_out);
  and and_22 (and_22_out, not_12_out, 1'b1);
  and Neg (Neg_out, or_1_out, and_1_out);
  and Pos (Pos_out, not_7_out, not_8_out);
  and and_23 (Zero, and_11_out, Clock);
  xor xor_5 (xor_5_out, not_12_out, 1'b1);
  and and_24 (and_24_out, AOUT1, Neg_out);
  and and_25 (and_25_out, Pos_out, AOUT1);
  and and_26 (and_26_out, not_13_out, not_9_out, fulladder_1_c);
  not not_13 (not_13_out, cmd);
  not not_14 (not_14_out, fulladder_1_c);
  and and_27 (and_27_out, and_24_out, not_14_out);
  or or_5 (or_5_out, and_26_out, and_25_out, and_27_out);
  not not_15 (not_15_out, Zero);
  and notZero (Overflow, or_5_out, not_15_out);

  assign Negative = AOUT1;

  // Notes on the sheet:
  //   Add/Sub command
  //   0 add, 1 sub
  //   B Input
  //   A-out output
  //   A Input
  //   Adder
  //   2's Complement
  //   Status output
  //   -8 + -8 is underflow (not supported)
endmodule

module fullAdder (
  input  A,
  input  B,
  input  Carry,
  output C,
  output Sum
);

  wire and_1_out, and_2_out, xor_1_out;

  and and_1 (and_1_out, A, B);
  xor xor_1 (xor_1_out, A, B);
  and and_2 (and_2_out, xor_1_out, Carry);
  or or_1 (C, and_1_out, and_2_out);
  xor xor_2 (Sum, xor_1_out, Carry);
endmodule

module Registers (
  input  InstrAddr1,
  input  InstrAddr2,
  input  InstrAddr3,
  input  Mode,
  input  DataInput1,
  input  DataInput2,
  input  DataInput3,
  input  DataInput4,
  output Out1,
  output Out2,
  output Out3,
  output Out4
);

  wire and_1_out, and_2_out, and_3_out, and_4_out, and_5_out, and_6_out, and_7_out, and_8_out, and_9_out,
       and_10_out, and_11_out, and_12_out, and_13_out, and_14_out, and_15_out, and_16_out, and_17_out,
       and_18_out, and_19_out, and_20_out, and_21_out, and_22_out, and_23_out, and_24_out, and_25_out,
       and_26_out, and_27_out, and_28_out, and_29_out, and_30_out, and_31_out, and_32_out, and_33_out,
       and_34_out, and_35_out, and_36_out, and_37_out, and_38_out, and_39_out, and_40_out, and_41_out,
       and_42_out, and_43_out, and_44_out, and_45_out, and_46_out, and_47_out, and_48_out, and_49_out,
       and_50_out, and_51_out, and_52_out, and_53_out, and_54_out, and_55_out, and_56_out, and_57_out,
       and_58_out, and_59_out, and_60_out, and_61_out, and_62_out, and_63_out, and_64_out, and_65_out,
       and_66_out, and_67_out, and_68_out, and_69_out, and_70_out, and_71_out, and_72_out, and_73_out,
       and_74_out, and_75_out, and_76_out, and_77_out, and_78_out, and_79_out, and_80_out, clock_1_out,
       d_ff_1_q, d_ff_2_q, d_ff_3_q, d_ff_4_q, d_ff_5_q, d_ff_6_q, d_ff_7_q, d_ff_8_q, d_ff_9_q, d_ff_10_q,
       d_ff_11_q, d_ff_12_q, d_ff_13_q, d_ff_14_q, d_ff_16_q, d_ff_17_q, d_ff_18_q, d_ff_19_q, d_ff_20_q,
       d_ff_21_q, d_ff_22_q, d_ff_23_q, d_ff_24_q, d_ff_26_q, d_ff_29_q, d_ff_30_q, d_ff_31_q, d_ff_32_q,
       d_ff_33_q, d_ff_34_q, d_ff_35_q, d_ff_36_q, d_ff_37_q, d_ff_38_q, d_ff_39_q, d_ff_40_q, d_ff_41_q,
       d_ff_42_q, d_ff_43_q, d_ff_44_q, not_1_out, not_2_out, not_3_out, not_4_out, not_5_out, not_6_out,
       not_7_out, not_8_out, not_9_out, not_10_out, not_11_out, not_12_out, not_13_out, or_1_out, or_2_out,
       or_3_out, or_4_out;

  D_Flip_Flop #(.trigger("falling")) d_ff_1 (
    .D(InstrAddr1), .clk(clock_1_out), .Q(d_ff_1_q));  // open: Qn, preset, reset
  Clock clock_1 (.out(clock_1_out));
  D_Flip_Flop #(.trigger("falling")) d_ff_2 (
    .D(InstrAddr2), .clk(clock_1_out), .Q(d_ff_2_q));  // open: Qn, preset, reset
  and and_1 (and_1_out, d_ff_1_q, d_ff_2_q, clock_1_out, d_ff_3_q);
  and and_2 (and_2_out, d_ff_1_q, d_ff_2_q, clock_1_out, not_1_out);
  not not_1 (not_1_out, d_ff_3_q);
  not not_2 (not_2_out, d_ff_2_q);
  and and_3 (and_3_out, d_ff_1_q, not_2_out, clock_1_out, d_ff_3_q);
  not not_3 (not_3_out, d_ff_2_q);
  and and_4 (and_4_out, d_ff_1_q, not_3_out, clock_1_out, not_4_out);
  not not_4 (not_4_out, d_ff_3_q);
  not not_5 (not_5_out, d_ff_1_q);
  and and_5 (and_5_out, not_5_out, d_ff_2_q, clock_1_out, d_ff_3_q);
  not not_6 (not_6_out, d_ff_1_q);
  and and_6 (and_6_out, not_6_out, d_ff_2_q, clock_1_out, not_7_out);
  not not_7 (not_7_out, d_ff_3_q);
  not not_8 (not_8_out, d_ff_1_q);
  not not_9 (not_9_out, d_ff_2_q);
  and and_7 (and_7_out, not_8_out, not_9_out, clock_1_out, d_ff_3_q);
  not not_10 (not_10_out, d_ff_1_q);
  not not_11 (not_11_out, d_ff_2_q);
  not not_12 (not_12_out, d_ff_3_q);
  D_Flip_Flop #(.trigger("falling")) d_ff_3 (
    .D(InstrAddr3), .clk(clock_1_out), .Q(d_ff_3_q));  // open: Qn, preset, reset
  and and_8 (and_8_out, and_1_out, not_13_out);
  and and_9 (and_9_out, and_2_out, not_13_out);
  and and_10 (and_10_out, and_3_out, not_13_out);
  and and_11 (and_11_out, and_4_out, not_13_out);
  and and_12 (and_12_out, and_5_out, not_13_out);
  and and_13 (and_13_out, and_6_out, not_13_out);
  and and_14 (and_14_out, and_7_out, not_13_out);
  and and_15 (and_15_out, not_10_out, not_11_out, clock_1_out, not_12_out);
  and and_16 (and_16_out, and_15_out, not_13_out);
  not not_13 (not_13_out, d_ff_4_q);
  D_Flip_Flop #(.trigger("falling")) d_ff_4 (.D(Mode), .clk(clock_1_out), .Q(d_ff_4_q));  // open: Qn, preset, reset
  and and_17 (and_17_out, and_1_out, not_13_out, d_ff_13_q);
  D_Flip_Flop #(.trigger("high")) d_ff_5 (.D(and_17_out), .clk(and_8_out), .Q(d_ff_5_q));  // open: Qn, preset, reset
  and and_18 (and_18_out, and_2_out, not_13_out, d_ff_13_q);
  D_Flip_Flop #(.trigger("high")) d_ff_6 (.D(and_18_out), .clk(and_9_out), .Q(d_ff_6_q));  // open: Qn, preset, reset
  and and_19 (and_19_out, and_3_out, not_13_out, d_ff_13_q);
  D_Flip_Flop #(.trigger("high")) d_ff_7 (.D(and_19_out), .clk(and_10_out), .Q(d_ff_7_q));  // open: Qn, preset, reset
  and and_20 (and_20_out, and_4_out, not_13_out, d_ff_13_q);
  D_Flip_Flop #(.trigger("high")) d_ff_8 (.D(and_20_out), .clk(and_11_out), .Q(d_ff_8_q));  // open: Qn, preset, reset
  and and_21 (and_21_out, and_5_out, not_13_out, d_ff_13_q);
  D_Flip_Flop #(.trigger("high")) d_ff_9 (.D(and_21_out), .clk(and_12_out), .Q(d_ff_9_q));  // open: Qn, preset, reset
  and and_22 (and_22_out, and_6_out, not_13_out, d_ff_13_q);
  D_Flip_Flop #(.trigger("high")) d_ff_10 (.D(and_22_out), .clk(and_13_out), .Q(d_ff_10_q));  // open: Qn, preset, reset
  and and_23 (and_23_out, and_7_out, not_13_out, d_ff_13_q);
  D_Flip_Flop #(.trigger("high")) d_ff_11 (.D(and_23_out), .clk(and_14_out), .Q(d_ff_11_q));  // open: Qn, preset, reset
  and and_24 (and_24_out, and_15_out, not_13_out, d_ff_13_q);
  D_Flip_Flop #(.trigger("high")) d_ff_12 (.D(and_24_out), .clk(and_16_out), .Q(d_ff_12_q));  // open: Qn, preset, reset
  or or_1 (or_1_out, and_25_out, and_26_out, and_27_out, and_28_out, and_29_out, and_30_out, and_31_out, and_32_out);
  and and_25 (and_25_out, d_ff_5_q, and_1_out, d_ff_4_q);
  and and_26 (and_26_out, d_ff_6_q, and_2_out, d_ff_4_q);
  and and_27 (and_27_out, d_ff_7_q, and_3_out, d_ff_4_q);
  and and_28 (and_28_out, d_ff_8_q, and_4_out, d_ff_4_q);
  and and_29 (and_29_out, d_ff_9_q, and_5_out, d_ff_4_q);
  and and_30 (and_30_out, d_ff_10_q, and_6_out, d_ff_4_q);
  and and_31 (and_31_out, d_ff_11_q, and_7_out, d_ff_4_q);
  and and_32 (and_32_out, d_ff_12_q, and_15_out, d_ff_4_q);
  D_Flip_Flop #(.trigger("falling")) d_ff_13 (
    .D(DataInput1), .clk(clock_1_out), .Q(d_ff_13_q));  // open: Qn, preset, reset
  D_Flip_Flop #(.trigger("falling")) d_ff_14 (
    .D(DataInput2), .clk(clock_1_out), .Q(d_ff_14_q));  // open: Qn, preset, reset
  D_Flip_Flop #(.trigger("high")) d_ff_15 (.D(or_1_out), .clk(clock_1_out), .Q(Out1));  // open: Qn, preset, reset
  and and_33 (and_33_out, and_1_out, not_13_out, d_ff_14_q);
  D_Flip_Flop #(.trigger("high")) d_ff_16 (.D(and_33_out), .clk(and_8_out), .Q(d_ff_16_q));  // open: Qn, preset, reset
  and and_34 (and_34_out, and_2_out, not_13_out, d_ff_14_q);
  D_Flip_Flop #(.trigger("high")) d_ff_17 (.D(and_34_out), .clk(and_9_out), .Q(d_ff_17_q));  // open: Qn, preset, reset
  and and_35 (and_35_out, and_3_out, not_13_out, d_ff_14_q);
  D_Flip_Flop #(.trigger("high")) d_ff_18 (.D(and_35_out), .clk(and_10_out), .Q(d_ff_18_q));  // open: Qn, preset, reset
  and and_36 (and_36_out, and_4_out, not_13_out, d_ff_14_q);
  D_Flip_Flop #(.trigger("high")) d_ff_19 (.D(and_36_out), .clk(and_11_out), .Q(d_ff_19_q));  // open: Qn, preset, reset
  and and_37 (and_37_out, and_5_out, not_13_out, d_ff_14_q);
  D_Flip_Flop #(.trigger("high")) d_ff_20 (.D(and_37_out), .clk(and_12_out), .Q(d_ff_20_q));  // open: Qn, preset, reset
  and and_38 (and_38_out, and_6_out, not_13_out, d_ff_14_q);
  D_Flip_Flop #(.trigger("high")) d_ff_21 (.D(and_38_out), .clk(and_13_out), .Q(d_ff_21_q));  // open: Qn, preset, reset
  and and_39 (and_39_out, and_7_out, not_13_out, d_ff_14_q);
  D_Flip_Flop #(.trigger("high")) d_ff_22 (.D(and_39_out), .clk(and_14_out), .Q(d_ff_22_q));  // open: Qn, preset, reset
  and and_40 (and_40_out, and_15_out, not_13_out, d_ff_14_q);
  D_Flip_Flop #(.trigger("high")) d_ff_23 (.D(and_40_out), .clk(and_16_out), .Q(d_ff_23_q));  // open: Qn, preset, reset
  D_Flip_Flop #(.trigger("falling")) d_ff_24 (
    .D(DataInput3), .clk(clock_1_out), .Q(d_ff_24_q));  // open: Qn, preset, reset
  D_Flip_Flop #(.trigger("high")) d_ff_25 (.D(or_2_out), .clk(clock_1_out), .Q(Out2));  // open: Qn, preset, reset
  or or_2 (or_2_out, and_41_out, and_42_out, and_43_out, and_44_out, and_45_out, and_46_out, and_47_out, and_48_out);
  and and_41 (and_41_out, d_ff_16_q, and_1_out, d_ff_4_q);
  and and_42 (and_42_out, d_ff_17_q, and_2_out, d_ff_4_q);
  and and_43 (and_43_out, d_ff_18_q, and_3_out, d_ff_4_q);
  and and_44 (and_44_out, d_ff_19_q, and_4_out, d_ff_4_q);
  and and_45 (and_45_out, d_ff_20_q, and_5_out, d_ff_4_q);
  and and_46 (and_46_out, d_ff_21_q, and_6_out, d_ff_4_q);
  and and_47 (and_47_out, d_ff_22_q, and_7_out, d_ff_4_q);
  and and_48 (and_48_out, d_ff_23_q, and_15_out, d_ff_4_q);
  D_Flip_Flop #(.trigger("falling")) d_ff_26 (
    .D(DataInput4), .clk(clock_1_out), .Q(d_ff_26_q));  // open: Qn, preset, reset
  D_Flip_Flop #(.trigger("high")) d_ff_27 (.D(or_3_out), .clk(clock_1_out), .Q(Out3));  // open: Qn, preset, reset
  D_Flip_Flop #(.trigger("high")) d_ff_28 (.D(or_4_out), .clk(clock_1_out), .Q(Out4));  // open: Qn, preset, reset
  and and_49 (and_49_out, and_1_out, not_13_out, d_ff_24_q);
  and and_50 (and_50_out, and_2_out, not_13_out, d_ff_24_q);
  and and_51 (and_51_out, and_3_out, not_13_out, d_ff_24_q);
  and and_52 (and_52_out, and_4_out, not_13_out, d_ff_24_q);
  and and_53 (and_53_out, and_5_out, not_13_out, d_ff_24_q);
  and and_54 (and_54_out, and_6_out, not_13_out, d_ff_24_q);
  and and_55 (and_55_out, and_7_out, not_13_out, d_ff_24_q);
  and and_56 (and_56_out, and_15_out, not_13_out, d_ff_24_q);
  or or_3 (or_3_out, and_57_out, and_58_out, and_59_out, and_60_out, and_61_out, and_62_out, and_63_out, and_64_out);
  and and_57 (and_57_out, d_ff_29_q, and_1_out, d_ff_4_q);
  D_Flip_Flop #(.trigger("high")) d_ff_29 (.D(and_49_out), .clk(and_8_out), .Q(d_ff_29_q));  // open: Qn, preset, reset
  and and_58 (and_58_out, d_ff_30_q, and_2_out, d_ff_4_q);
  D_Flip_Flop #(.trigger("high")) d_ff_30 (.D(and_50_out), .clk(and_9_out), .Q(d_ff_30_q));  // open: Qn, preset, reset
  and and_59 (and_59_out, d_ff_31_q, and_3_out, d_ff_4_q);
  D_Flip_Flop #(.trigger("high")) d_ff_31 (.D(and_51_out), .clk(and_10_out), .Q(d_ff_31_q));  // open: Qn, preset, reset
  and and_60 (and_60_out, d_ff_32_q, and_4_out, d_ff_4_q);
  D_Flip_Flop #(.trigger("high")) d_ff_32 (.D(and_52_out), .clk(and_11_out), .Q(d_ff_32_q));  // open: Qn, preset, reset
  and and_61 (and_61_out, d_ff_33_q, and_5_out, d_ff_4_q);
  D_Flip_Flop #(.trigger("high")) d_ff_33 (.D(and_53_out), .clk(and_12_out), .Q(d_ff_33_q));  // open: Qn, preset, reset
  and and_62 (and_62_out, d_ff_34_q, and_6_out, d_ff_4_q);
  D_Flip_Flop #(.trigger("high")) d_ff_34 (.D(and_54_out), .clk(and_13_out), .Q(d_ff_34_q));  // open: Qn, preset, reset
  and and_63 (and_63_out, d_ff_35_q, and_7_out, d_ff_4_q);
  D_Flip_Flop #(.trigger("high")) d_ff_35 (.D(and_55_out), .clk(and_14_out), .Q(d_ff_35_q));  // open: Qn, preset, reset
  and and_64 (and_64_out, d_ff_36_q, and_15_out, d_ff_4_q);
  D_Flip_Flop #(.trigger("high")) d_ff_36 (.D(and_56_out), .clk(and_16_out), .Q(d_ff_36_q));  // open: Qn, preset, reset
  and and_65 (and_65_out, and_1_out, not_13_out, d_ff_26_q);
  D_Flip_Flop #(.trigger("high")) d_ff_37 (.D(and_65_out), .clk(and_8_out), .Q(d_ff_37_q));  // open: Qn, preset, reset
  and and_66 (and_66_out, and_2_out, not_13_out, d_ff_26_q);
  D_Flip_Flop #(.trigger("high")) d_ff_38 (.D(and_66_out), .clk(and_9_out), .Q(d_ff_38_q));  // open: Qn, preset, reset
  and and_67 (and_67_out, and_3_out, not_13_out, d_ff_26_q);
  D_Flip_Flop #(.trigger("high")) d_ff_39 (.D(and_67_out), .clk(and_10_out), .Q(d_ff_39_q));  // open: Qn, preset, reset
  and and_68 (and_68_out, and_4_out, not_13_out, d_ff_26_q);
  D_Flip_Flop #(.trigger("high")) d_ff_40 (.D(and_68_out), .clk(and_11_out), .Q(d_ff_40_q));  // open: Qn, preset, reset
  and and_69 (and_69_out, and_5_out, not_13_out, d_ff_26_q);
  D_Flip_Flop #(.trigger("high")) d_ff_41 (.D(and_69_out), .clk(and_12_out), .Q(d_ff_41_q));  // open: Qn, preset, reset
  and and_70 (and_70_out, and_6_out, not_13_out, d_ff_26_q);
  D_Flip_Flop #(.trigger("high")) d_ff_42 (.D(and_70_out), .clk(and_13_out), .Q(d_ff_42_q));  // open: Qn, preset, reset
  and and_71 (and_71_out, and_7_out, not_13_out, d_ff_26_q);
  D_Flip_Flop #(.trigger("high")) d_ff_43 (.D(and_71_out), .clk(and_14_out), .Q(d_ff_43_q));  // open: Qn, preset, reset
  and and_72 (and_72_out, and_15_out, not_13_out, d_ff_26_q);
  D_Flip_Flop #(.trigger("high")) d_ff_44 (.D(and_72_out), .clk(and_16_out), .Q(d_ff_44_q));  // open: Qn, preset, reset
  or or_4 (or_4_out, and_73_out, and_74_out, and_75_out, and_76_out, and_77_out, and_78_out, and_79_out, and_80_out);
  and and_73 (and_73_out, d_ff_37_q, and_1_out, d_ff_4_q);
  and and_74 (and_74_out, d_ff_38_q, and_2_out, d_ff_4_q);
  and and_75 (and_75_out, d_ff_39_q, and_3_out, d_ff_4_q);
  and and_76 (and_76_out, d_ff_40_q, and_4_out, d_ff_4_q);
  and and_77 (and_77_out, d_ff_41_q, and_5_out, d_ff_4_q);
  and and_78 (and_78_out, d_ff_42_q, and_6_out, d_ff_4_q);
  and and_79 (and_79_out, d_ff_43_q, and_7_out, d_ff_4_q);
  and and_80 (and_80_out, d_ff_44_q, and_15_out, d_ff_4_q);

  // Notes on the sheet:
  //   3-bit address input pins
  //   Mode input pin
  //   4-bit data input pins
endmodule

module PC (
);

  wire undriven;

  D_Flip_Flop d_ff_1 (.D(undriven));  // open: clk, Q, Qn, preset, reset
  D_Flip_Flop d_ff_2 ();  // open: D, clk, Q, Qn, preset, reset
  D_Flip_Flop d_ff_3 ();  // open: D, clk, Q, Qn, preset, reset
  D_Flip_Flop d_ff_4 ();  // open: D, clk, Q, Qn, preset, reset
  D_Flip_Flop d_ff_5 ();  // open: D, clk, Q, Qn, preset, reset
  D_Flip_Flop d_ff_6 ();  // open: D, clk, Q, Qn, preset, reset
  D_Flip_Flop d_ff_7 ();  // open: D, clk, Q, Qn, preset, reset
  D_Flip_Flop d_ff_8 ();  // open: D, clk, Q, Qn, preset, reset
endmodule

module dataRAM (
  input  InstrAddr1,
  input  InstrAddr2,
  input  InstrAddr3,
  input  Mode,
  input  DataInput1,
  input  DataInput2,
  input  DataInput3,
  input  DataInput4,
  output IrOut1,
  output IrOut2,
  output IrOut3,
  output IrOut4
);

  wire and_1_out, and_2_out, and_3_out, and_4_out, and_5_out, and_6_out, and_7_out, and_8_out, and_9_out,
       and_10_out, and_11_out, and_12_out, and_13_out, and_14_out, and_15_out, and_16_out, and_17_out,
       and_18_out, and_19_out, and_20_out, and_21_out, and_22_out, and_23_out, and_24_out, and_25_out,
       and_26_out, and_27_out, and_28_out, and_29_out, and_30_out, and_31_out, and_32_out, and_33_out,
       and_34_out, and_35_out, and_36_out, and_37_out, and_38_out, and_39_out, and_40_out, and_41_out,
       and_42_out, and_43_out, and_44_out, and_45_out, and_46_out, and_47_out, and_48_out, and_49_out,
       and_50_out, and_51_out, and_52_out, and_53_out, and_54_out, and_55_out, and_56_out, and_57_out,
       and_58_out, and_59_out, and_60_out, and_61_out, and_62_out, and_63_out, and_64_out, and_65_out,
       and_66_out, and_67_out, and_68_out, and_69_out, and_70_out, and_71_out, and_72_out, and_73_out,
       and_74_out, and_75_out, and_76_out, and_77_out, and_78_out, and_79_out, and_80_out, clock_1_out,
       d_ff_1_q, d_ff_2_q, d_ff_3_q, d_ff_4_q, d_ff_5_q, d_ff_6_q, d_ff_7_q, d_ff_8_q, d_ff_9_q, d_ff_10_q,
       d_ff_11_q, d_ff_12_q, d_ff_13_q, d_ff_14_q, d_ff_16_q, d_ff_17_q, d_ff_18_q, d_ff_19_q, d_ff_20_q,
       d_ff_21_q, d_ff_22_q, d_ff_23_q, d_ff_24_q, d_ff_26_q, d_ff_29_q, d_ff_30_q, d_ff_31_q, d_ff_32_q,
       d_ff_33_q, d_ff_34_q, d_ff_35_q, d_ff_36_q, d_ff_37_q, d_ff_38_q, d_ff_39_q, d_ff_40_q, d_ff_41_q,
       d_ff_42_q, d_ff_43_q, d_ff_44_q, not_1_out, not_2_out, not_3_out, not_4_out, not_5_out, not_6_out,
       not_7_out, not_8_out, not_9_out, not_10_out, not_11_out, not_12_out, not_13_out, or_1_out, or_2_out,
       or_3_out, or_4_out;

  D_Flip_Flop #(.trigger("falling")) d_ff_1 (
    .D(InstrAddr1), .clk(clock_1_out), .Q(d_ff_1_q));  // open: Qn, preset, reset
  Clock clock_1 (.out(clock_1_out));
  D_Flip_Flop #(.trigger("falling")) d_ff_2 (
    .D(InstrAddr2), .clk(clock_1_out), .Q(d_ff_2_q));  // open: Qn, preset, reset
  and and_1 (and_1_out, d_ff_1_q, d_ff_2_q, clock_1_out, d_ff_3_q);
  and and_2 (and_2_out, d_ff_1_q, d_ff_2_q, clock_1_out, not_1_out);
  not not_1 (not_1_out, d_ff_3_q);
  not not_2 (not_2_out, d_ff_2_q);
  and and_3 (and_3_out, d_ff_1_q, not_2_out, clock_1_out, d_ff_3_q);
  not not_3 (not_3_out, d_ff_2_q);
  and and_4 (and_4_out, d_ff_1_q, not_3_out, clock_1_out, not_4_out);
  not not_4 (not_4_out, d_ff_3_q);
  not not_5 (not_5_out, d_ff_1_q);
  and and_5 (and_5_out, not_5_out, d_ff_2_q, clock_1_out, d_ff_3_q);
  not not_6 (not_6_out, d_ff_1_q);
  and and_6 (and_6_out, not_6_out, d_ff_2_q, clock_1_out, not_7_out);
  not not_7 (not_7_out, d_ff_3_q);
  not not_8 (not_8_out, d_ff_1_q);
  not not_9 (not_9_out, d_ff_2_q);
  and and_7 (and_7_out, not_8_out, not_9_out, clock_1_out, d_ff_3_q);
  not not_10 (not_10_out, d_ff_1_q);
  not not_11 (not_11_out, d_ff_2_q);
  not not_12 (not_12_out, d_ff_3_q);
  D_Flip_Flop #(.trigger("falling")) d_ff_3 (
    .D(InstrAddr3), .clk(clock_1_out), .Q(d_ff_3_q));  // open: Qn, preset, reset
  and and_8 (and_8_out, and_1_out, not_13_out);
  and and_9 (and_9_out, and_2_out, not_13_out);
  and and_10 (and_10_out, and_3_out, not_13_out);
  and and_11 (and_11_out, and_4_out, not_13_out);
  and and_12 (and_12_out, and_5_out, not_13_out);
  and and_13 (and_13_out, and_6_out, not_13_out);
  and and_14 (and_14_out, and_7_out, not_13_out);
  and and_15 (and_15_out, not_10_out, not_11_out, clock_1_out, not_12_out);
  and and_16 (and_16_out, and_15_out, not_13_out);
  not not_13 (not_13_out, d_ff_4_q);
  D_Flip_Flop #(.trigger("falling")) d_ff_4 (.D(Mode), .clk(clock_1_out), .Q(d_ff_4_q));  // open: Qn, preset, reset
  and and_17 (and_17_out, and_1_out, not_13_out, d_ff_13_q);
  D_Flip_Flop #(.trigger("high")) d_ff_5 (.D(and_17_out), .clk(and_8_out), .Q(d_ff_5_q));  // open: Qn, preset, reset
  and and_18 (and_18_out, and_2_out, not_13_out, d_ff_13_q);
  D_Flip_Flop #(.trigger("high")) d_ff_6 (.D(and_18_out), .clk(and_9_out), .Q(d_ff_6_q));  // open: Qn, preset, reset
  and and_19 (and_19_out, and_3_out, not_13_out, d_ff_13_q);
  D_Flip_Flop #(.trigger("high")) d_ff_7 (.D(and_19_out), .clk(and_10_out), .Q(d_ff_7_q));  // open: Qn, preset, reset
  and and_20 (and_20_out, and_4_out, not_13_out, d_ff_13_q);
  D_Flip_Flop #(.trigger("high")) d_ff_8 (.D(and_20_out), .clk(and_11_out), .Q(d_ff_8_q));  // open: Qn, preset, reset
  and and_21 (and_21_out, and_5_out, not_13_out, d_ff_13_q);
  D_Flip_Flop #(.trigger("high")) d_ff_9 (.D(and_21_out), .clk(and_12_out), .Q(d_ff_9_q));  // open: Qn, preset, reset
  and and_22 (and_22_out, and_6_out, not_13_out, d_ff_13_q);
  D_Flip_Flop #(.trigger("high")) d_ff_10 (.D(and_22_out), .clk(and_13_out), .Q(d_ff_10_q));  // open: Qn, preset, reset
  and and_23 (and_23_out, and_7_out, not_13_out, d_ff_13_q);
  D_Flip_Flop #(.trigger("high")) d_ff_11 (.D(and_23_out), .clk(and_14_out), .Q(d_ff_11_q));  // open: Qn, preset, reset
  and and_24 (and_24_out, and_15_out, not_13_out, d_ff_13_q);
  D_Flip_Flop #(.trigger("high")) d_ff_12 (.D(and_24_out), .clk(and_16_out), .Q(d_ff_12_q));  // open: Qn, preset, reset
  or or_1 (or_1_out, and_25_out, and_26_out, and_27_out, and_28_out, and_29_out, and_30_out, and_31_out, and_32_out);
  and and_25 (and_25_out, d_ff_5_q, and_1_out, d_ff_4_q);
  and and_26 (and_26_out, d_ff_6_q, and_2_out, d_ff_4_q);
  and and_27 (and_27_out, d_ff_7_q, and_3_out, d_ff_4_q);
  and and_28 (and_28_out, d_ff_8_q, and_4_out, d_ff_4_q);
  and and_29 (and_29_out, d_ff_9_q, and_5_out, d_ff_4_q);
  and and_30 (and_30_out, d_ff_10_q, and_6_out, d_ff_4_q);
  and and_31 (and_31_out, d_ff_11_q, and_7_out, d_ff_4_q);
  and and_32 (and_32_out, d_ff_12_q, and_15_out, d_ff_4_q);
  D_Flip_Flop #(.trigger("falling")) d_ff_13 (
    .D(DataInput1), .clk(clock_1_out), .Q(d_ff_13_q));  // open: Qn, preset, reset
  D_Flip_Flop #(.trigger("falling")) d_ff_14 (
    .D(DataInput2), .clk(clock_1_out), .Q(d_ff_14_q));  // open: Qn, preset, reset
  D_Flip_Flop #(.trigger("high")) d_ff_15 (.D(or_1_out), .clk(clock_1_out), .Q(IrOut1));  // open: Qn, preset, reset
  and and_33 (and_33_out, and_1_out, not_13_out, d_ff_14_q);
  D_Flip_Flop #(.trigger("high")) d_ff_16 (.D(and_33_out), .clk(and_8_out), .Q(d_ff_16_q));  // open: Qn, preset, reset
  and and_34 (and_34_out, and_2_out, not_13_out, d_ff_14_q);
  D_Flip_Flop #(.trigger("high")) d_ff_17 (.D(and_34_out), .clk(and_9_out), .Q(d_ff_17_q));  // open: Qn, preset, reset
  and and_35 (and_35_out, and_3_out, not_13_out, d_ff_14_q);
  D_Flip_Flop #(.trigger("high")) d_ff_18 (.D(and_35_out), .clk(and_10_out), .Q(d_ff_18_q));  // open: Qn, preset, reset
  and and_36 (and_36_out, and_4_out, not_13_out, d_ff_14_q);
  D_Flip_Flop #(.trigger("high")) d_ff_19 (.D(and_36_out), .clk(and_11_out), .Q(d_ff_19_q));  // open: Qn, preset, reset
  and and_37 (and_37_out, and_5_out, not_13_out, d_ff_14_q);
  D_Flip_Flop #(.trigger("high")) d_ff_20 (.D(and_37_out), .clk(and_12_out), .Q(d_ff_20_q));  // open: Qn, preset, reset
  and and_38 (and_38_out, and_6_out, not_13_out, d_ff_14_q);
  D_Flip_Flop #(.trigger("high")) d_ff_21 (.D(and_38_out), .clk(and_13_out), .Q(d_ff_21_q));  // open: Qn, preset, reset
  and and_39 (and_39_out, and_7_out, not_13_out, d_ff_14_q);
  D_Flip_Flop #(.trigger("high")) d_ff_22 (.D(and_39_out), .clk(and_14_out), .Q(d_ff_22_q));  // open: Qn, preset, reset
  and and_40 (and_40_out, and_15_out, not_13_out, d_ff_14_q);
  D_Flip_Flop #(.trigger("high")) d_ff_23 (.D(and_40_out), .clk(and_16_out), .Q(d_ff_23_q));  // open: Qn, preset, reset
  D_Flip_Flop #(.trigger("falling")) d_ff_24 (
    .D(DataInput3), .clk(clock_1_out), .Q(d_ff_24_q));  // open: Qn, preset, reset
  D_Flip_Flop #(.trigger("high")) d_ff_25 (.D(or_2_out), .clk(clock_1_out), .Q(IrOut2));  // open: Qn, preset, reset
  or or_2 (or_2_out, and_41_out, and_42_out, and_43_out, and_44_out, and_45_out, and_46_out, and_47_out, and_48_out);
  and and_41 (and_41_out, d_ff_16_q, and_1_out, d_ff_4_q);
  and and_42 (and_42_out, d_ff_17_q, and_2_out, d_ff_4_q);
  and and_43 (and_43_out, d_ff_18_q, and_3_out, d_ff_4_q);
  and and_44 (and_44_out, d_ff_19_q, and_4_out, d_ff_4_q);
  and and_45 (and_45_out, d_ff_20_q, and_5_out, d_ff_4_q);
  and and_46 (and_46_out, d_ff_21_q, and_6_out, d_ff_4_q);
  and and_47 (and_47_out, d_ff_22_q, and_7_out, d_ff_4_q);
  and and_48 (and_48_out, d_ff_23_q, and_15_out, d_ff_4_q);
  D_Flip_Flop #(.trigger("falling")) d_ff_26 (
    .D(DataInput4), .clk(clock_1_out), .Q(d_ff_26_q));  // open: Qn, preset, reset
  D_Flip_Flop #(.trigger("high")) d_ff_27 (.D(or_3_out), .clk(clock_1_out), .Q(IrOut3));  // open: Qn, preset, reset
  D_Flip_Flop #(.trigger("high")) d_ff_28 (.D(or_4_out), .clk(clock_1_out), .Q(IrOut4));  // open: Qn, preset, reset
  and and_49 (and_49_out, and_1_out, not_13_out, d_ff_24_q);
  and and_50 (and_50_out, and_2_out, not_13_out, d_ff_24_q);
  and and_51 (and_51_out, and_3_out, not_13_out, d_ff_24_q);
  and and_52 (and_52_out, and_4_out, not_13_out, d_ff_24_q);
  and and_53 (and_53_out, and_5_out, not_13_out, d_ff_24_q);
  and and_54 (and_54_out, and_6_out, not_13_out, d_ff_24_q);
  and and_55 (and_55_out, and_7_out, not_13_out, d_ff_24_q);
  and and_56 (and_56_out, and_15_out, not_13_out, d_ff_24_q);
  or or_3 (or_3_out, and_57_out, and_58_out, and_59_out, and_60_out, and_61_out, and_62_out, and_63_out, and_64_out);
  and and_57 (and_57_out, d_ff_29_q, and_1_out, d_ff_4_q);
  D_Flip_Flop #(.trigger("high")) d_ff_29 (.D(and_49_out), .clk(and_8_out), .Q(d_ff_29_q));  // open: Qn, preset, reset
  and and_58 (and_58_out, d_ff_30_q, and_2_out, d_ff_4_q);
  D_Flip_Flop #(.trigger("high")) d_ff_30 (.D(and_50_out), .clk(and_9_out), .Q(d_ff_30_q));  // open: Qn, preset, reset
  and and_59 (and_59_out, d_ff_31_q, and_3_out, d_ff_4_q);
  D_Flip_Flop #(.trigger("high")) d_ff_31 (.D(and_51_out), .clk(and_10_out), .Q(d_ff_31_q));  // open: Qn, preset, reset
  and and_60 (and_60_out, d_ff_32_q, and_4_out, d_ff_4_q);
  D_Flip_Flop #(.trigger("high")) d_ff_32 (.D(and_52_out), .clk(and_11_out), .Q(d_ff_32_q));  // open: Qn, preset, reset
  and and_61 (and_61_out, d_ff_33_q, and_5_out, d_ff_4_q);
  D_Flip_Flop #(.trigger("high")) d_ff_33 (.D(and_53_out), .clk(and_12_out), .Q(d_ff_33_q));  // open: Qn, preset, reset
  and and_62 (and_62_out, d_ff_34_q, and_6_out, d_ff_4_q);
  D_Flip_Flop #(.trigger("high")) d_ff_34 (.D(and_54_out), .clk(and_13_out), .Q(d_ff_34_q));  // open: Qn, preset, reset
  and and_63 (and_63_out, d_ff_35_q, and_7_out, d_ff_4_q);
  D_Flip_Flop #(.trigger("high")) d_ff_35 (.D(and_55_out), .clk(and_14_out), .Q(d_ff_35_q));  // open: Qn, preset, reset
  and and_64 (and_64_out, d_ff_36_q, and_15_out, d_ff_4_q);
  D_Flip_Flop #(.trigger("high")) d_ff_36 (.D(and_56_out), .clk(and_16_out), .Q(d_ff_36_q));  // open: Qn, preset, reset
  and and_65 (and_65_out, and_1_out, not_13_out, d_ff_26_q);
  D_Flip_Flop #(.trigger("high")) d_ff_37 (.D(and_65_out), .clk(and_8_out), .Q(d_ff_37_q));  // open: Qn, preset, reset
  and and_66 (and_66_out, and_2_out, not_13_out, d_ff_26_q);
  D_Flip_Flop #(.trigger("high")) d_ff_38 (.D(and_66_out), .clk(and_9_out), .Q(d_ff_38_q));  // open: Qn, preset, reset
  and and_67 (and_67_out, and_3_out, not_13_out, d_ff_26_q);
  D_Flip_Flop #(.trigger("high")) d_ff_39 (.D(and_67_out), .clk(and_10_out), .Q(d_ff_39_q));  // open: Qn, preset, reset
  and and_68 (and_68_out, and_4_out, not_13_out, d_ff_26_q);
  D_Flip_Flop #(.trigger("high")) d_ff_40 (.D(and_68_out), .clk(and_11_out), .Q(d_ff_40_q));  // open: Qn, preset, reset
  and and_69 (and_69_out, and_5_out, not_13_out, d_ff_26_q);
  D_Flip_Flop #(.trigger("high")) d_ff_41 (.D(and_69_out), .clk(and_12_out), .Q(d_ff_41_q));  // open: Qn, preset, reset
  and and_70 (and_70_out, and_6_out, not_13_out, d_ff_26_q);
  D_Flip_Flop #(.trigger("high")) d_ff_42 (.D(and_70_out), .clk(and_13_out), .Q(d_ff_42_q));  // open: Qn, preset, reset
  and and_71 (and_71_out, and_7_out, not_13_out, d_ff_26_q);
  D_Flip_Flop #(.trigger("high")) d_ff_43 (.D(and_71_out), .clk(and_14_out), .Q(d_ff_43_q));  // open: Qn, preset, reset
  and and_72 (and_72_out, and_15_out, not_13_out, d_ff_26_q);
  D_Flip_Flop #(.trigger("high")) d_ff_44 (.D(and_72_out), .clk(and_16_out), .Q(d_ff_44_q));  // open: Qn, preset, reset
  or or_4 (or_4_out, and_73_out, and_74_out, and_75_out, and_76_out, and_77_out, and_78_out, and_79_out, and_80_out);
  and and_73 (and_73_out, d_ff_37_q, and_1_out, d_ff_4_q);
  and and_74 (and_74_out, d_ff_38_q, and_2_out, d_ff_4_q);
  and and_75 (and_75_out, d_ff_39_q, and_3_out, d_ff_4_q);
  and and_76 (and_76_out, d_ff_40_q, and_4_out, d_ff_4_q);
  and and_77 (and_77_out, d_ff_41_q, and_5_out, d_ff_4_q);
  and and_78 (and_78_out, d_ff_42_q, and_6_out, d_ff_4_q);
  and and_79 (and_79_out, d_ff_43_q, and_7_out, d_ff_4_q);
  and and_80 (and_80_out, d_ff_44_q, and_15_out, d_ff_4_q);

  // Notes on the sheet:
  //   3-bit address input pins
  //   Mode input pin
  //   4-bit data input pins
endmodule

module MyALU (
  input  L1,
  input  L2,
  input  L3,
  input  L4,
  input  R1,
  input  R2,
  input  R3,
  input  R4,
  input  cmd,
  input  in_10,
  output out_11,
  output out_12,
  output out_13,
  output out1,
  output out2,
  output out3,
  output out4
);

  wire and_1_out, and_2_out, and_3_out, and_4_out, and_5_out, and_6_out, and_7_out, and_8_out, and_9_out,
       and_10_out, and_11_out, and_12_out, and_13_out, and_14_out, and_15_out, and_16_out, and_17_out,
       and_18_out, and_19_out, and_20_out, and_21_out, and_22_out, and_23_out, and_24_out, and_25_out,
       and_26_out, and_27_out, and_28_out, clock_1_out, d_ff_2_q, d_ff_5_q, d_ff_6_q, d_ff_8_q, d_ff_9_q,
       d_ff_10_q, d_ff_11_q, d_ff_12_q, d_ff_13_q, d_ff_14_q, not_1_out, not_2_out, not_3_out, not_4_out,
       not_5_out, not_6_out, not_7_out, not_8_out, not_9_out, not_10_out, not_11_out, not_12_out, not_13_out,
       not_14_out, not_15_out, or_1_out, or_2_out, or_3_out, or_4_out, or_5_out, or_6_out, or_7_out,
       or_8_out, or_9_out, or_10_out, or_11_out, or_12_out, or_13_out, or_14_out, xor_1_out, xor_2_out,
       xor_3_out, xor_4_out;

  Clock clock_1 (.out(clock_1_out));
  not not_1 (not_1_out, cmd);
  and and_1 (and_1_out, or_4_out, and_17_out);
  and and_2 (and_2_out, or_4_out, d_ff_5_q);
  or or_1 (or_1_out, and_1_out, and_2_out, and_3_out);
  and and_3 (and_3_out, and_17_out, d_ff_5_q);
  not not_2 (not_2_out, or_1_out);
  and and_4 (and_4_out, not_2_out, or_2_out);
  not not_3 (not_3_out, d_ff_5_q);
  and and_5 (and_5_out, or_3_out, not_3_out, not_4_out, not_1_out);
  not not_4 (not_4_out, and_17_out);
  or or_2 (or_2_out, or_4_out, and_17_out, d_ff_5_q);
  and and_6 (and_6_out, or_4_out, and_17_out, d_ff_5_q);
  or or_3 (or_3_out, and_4_out, and_6_out);
  and and_7 (and_7_out, or_7_out, and_20_out);
  and and_8 (and_8_out, or_7_out, d_ff_6_q);
  or or_4 (or_4_out, and_7_out, and_8_out, and_9_out);
  D_Flip_Flop d_ff_1 (.D(or_3_out), .clk(clock_1_out), .Q(out1));  // open: Qn, preset, reset
  D_Flip_Flop d_ff_2 (.D(cmd), .clk(clock_1_out), .Q(d_ff_2_q));  // open: Qn, preset, reset
  and and_9 (and_9_out, and_20_out, d_ff_6_q);
  not not_5 (not_5_out, or_4_out);
  D_Flip_Flop d_ff_3 (.D(or_6_out), .clk(clock_1_out), .Q(out2));  // open: Qn, preset, reset
  or or_5 (or_5_out, or_7_out, and_20_out, d_ff_6_q);
  and and_10 (and_10_out, not_5_out, or_5_out);
  or or_6 (or_6_out, and_10_out, and_11_out);
  D_Flip_Flop d_ff_4 (.D(or_9_out), .clk(clock_1_out), .Q(out3));  // open: Qn, preset, reset
  D_Flip_Flop d_ff_5 (.D(L1), .clk(clock_1_out), .Q(d_ff_5_q));  // open: Qn, preset, reset
  and and_11 (and_11_out, or_7_out, and_20_out, d_ff_6_q);
  D_Flip_Flop d_ff_6 (.D(L2), .clk(clock_1_out), .Q(d_ff_6_q));  // open: Qn, preset, reset
  and and_12 (and_12_out, and_23_out, and_22_out);
  D_Flip_Flop d_ff_7 (.D(and_25_out), .clk(clock_1_out), .Q(out4));  // open: Qn, preset, reset
  and and_13 (and_13_out, and_23_out, d_ff_8_q);
  and and_14 (and_14_out, and_22_out, d_ff_8_q);
  or or_7 (or_7_out, and_12_out, and_13_out, and_14_out);
  not not_6 (not_6_out, or_7_out);
  D_Flip_Flop d_ff_8 (.D(L3), .clk(clock_1_out), .Q(d_ff_8_q));  // open: Qn, preset, reset
  or or_8 (or_8_out, and_23_out, and_22_out, d_ff_8_q);
  and and_15 (and_15_out, not_6_out, or_8_out);
  D_Flip_Flop d_ff_9 (.D(L4), .clk(clock_1_out), .Q(d_ff_9_q));  // open: Qn, preset, reset
  and and_16 (and_16_out, and_19_out, xor_1_out);
  not not_7 (not_7_out, and_16_out);
  and and_17 (and_17_out, not_7_out, or_10_out);
  and and_18 (and_18_out, and_23_out, and_22_out, d_ff_8_q);
  or or_9 (or_9_out, and_15_out, and_18_out);
  or or_10 (or_10_out, and_19_out, xor_1_out);
  D_Flip_Flop d_ff_10 (.D(R1), .clk(clock_1_out), .Q(d_ff_10_q));  // open: Qn, preset, reset
  xor xor_1 (xor_1_out, d_ff_2_q, d_ff_10_q);
  and and_19 (and_19_out, and_21_out, xor_2_out);
  not not_8 (not_8_out, and_19_out);
  and and_20 (and_20_out, not_8_out, or_11_out);
  D_Flip_Flop d_ff_11 (.D(R2), .clk(clock_1_out), .Q(d_ff_11_q));  // open: Qn, preset, reset
  xor xor_2 (xor_2_out, d_ff_2_q, d_ff_11_q);
  or or_11 (or_11_out, and_21_out, xor_2_out);
  D_Flip_Flop d_ff_12 (.D(R3), .clk(clock_1_out), .Q(d_ff_12_q));  // open: Qn, preset, reset
  and and_21 (and_21_out, and_24_out, xor_3_out);
  or or_12 (or_12_out, and_24_out, xor_3_out);
  not not_9 (not_9_out, and_21_out);
  and and_22 (and_22_out, not_9_out, or_12_out);
  D_Flip_Flop d_ff_13 (.D(R4), .clk(clock_1_out), .Q(d_ff_13_q));  // open: Qn, preset, reset
  xor xor_3 (xor_3_out, d_ff_2_q, d_ff_12_q);
  and and_23 (and_23_out, d_ff_9_q, and_27_out);
  xor xor_4 (xor_4_out, d_ff_2_q, d_ff_13_q);
  and and_24 (and_24_out, and_26_out, xor_4_out);
  not not_10 (not_10_out, and_24_out);
  or or_13 (or_13_out, d_ff_9_q, and_27_out);
  not not_11 (not_11_out, and_23_out);
  and and_25 (and_25_out, not_11_out, or_13_out);
  and and_26 (and_26_out, d_ff_2_q, d_ff_14_q);
  or or_14 (or_14_out, and_26_out, xor_4_out);
  and and_27 (and_27_out, not_10_out, or_14_out);
  not not_12 (not_12_out, or_3_out);
  not not_13 (not_13_out, or_6_out);
  not not_14 (not_14_out, or_9_out);
  not not_15 (not_15_out, and_25_out);
  and and_28 (and_28_out, not_12_out, not_13_out, not_14_out, not_15_out);
  D_Flip_Flop d_ff_14 (.D(in_10), .clk(clock_1_out), .Q(d_ff_14_q));  // open: Qn, preset, reset
  D_Flip_Flop d_ff_15 (.D(or_3_out), .clk(clock_1_out), .Q(out_11));  // open: Qn, preset, reset
  D_Flip_Flop d_ff_16 (.D(and_28_out), .clk(clock_1_out), .Q(out_12));  // open: Qn, preset, reset
  D_Flip_Flop d_ff_17 (.D(and_5_out), .clk(clock_1_out), .Q(out_13));  // open: Qn, preset, reset

  // Notes on the sheet:
  //   Leticia Huang 261068858
  //   Add/Sub command
  //   A-out output
  //   L input
  //   R input
  //   Add 1 to 2's comp, plz turn to 1 before testing
  //   Status output
endmodule
