// Logisim project project.circ as structural Verilog: 7 circuits, main circuit main
module main (
  input  DataInput1,
  input  DataInput2,
  input  DataInput3,
  input  DataInput4,
  input  in_5,
  output out_6,
  output out_7,
  output out_8,
  output out_9
);

  wire add, add_or_sub_instr, ADD_TICK_1, ADD_TICK_2, ADD_TICK_3, ADD_TICK_4, alu_1_aout2, alu_1_aout3,
       alu_1_aout4, alu_2_aout3, alu_2_aout4, ALU_output_0, ALU_output_1, ALU_output_2, ALU_output_3,
       and_1_out, and_2_out, and_3_out, and_4_out, and_5_out, and_6_out, and_7_out, and_8_out, and_9_out,
       and_10_out, and_11_out, and_12_out, and_13_out, and_14_out, and_15_out, and_16_out, and_17_out,
       and_18_out, and_19_out, and_20_out, and_21_out, and_22_out, and_23_out, and_24_out, and_25_out,
       and_26_out, and_27_out, and_28_out, and_29_out, and_30_out, and_31_out, and_32_out, and_33_out,
       and_34_out, and_35_out, and_36_out, and_37_out, and_38_out, and_39_out, and_40_out, and_41_out,
       and_42_out, and_43_out, and_44_out, and_45_out, and_46_out, and_47_out, and_48_out, and_49_out,
       and_50_out, and_51_out, and_52_out, and_53_out, and_54_out, and_55_out, and_56_out, and_57_out,
       and_58_out, and_59_out, and_60_out, and_61_out, and_62_out, and_63_out, and_64_out, and_65_out,
       and_66_out, and_67_out, and_68_out, and_69_out, and_70_out, and_71_out, and_72_out, and_73_out,
       and_74_out, and_75_out, and_76_out, and_77_out, and_78_out, and_79_out, and_80_out, and_81_out,
       and_82_out, and_83_out, and_110_out, and_111_out, and_112_out, and_113_out, and_114_out, and_115_out,
       and_116_out, and_117_out, and_118_out, and_119_out, and_120_out, and_121_out, and_122_out,
       and_123_out, and_124_out, and_125_out, and_126_out, and_127_out, and_128_out, and_129_out,
       and_130_out, and_131_out, and_132_out, and_133_out, and_134_out, and_135_out, and_136_out,
       and_137_out, and_138_out, and_139_out, and_140_out, and_141_out, and_142_out, and_143_out,
       and_144_out, and_145_out, and_146_out, and_147_out, and_148_out, and_149_out, and_150_out,
       and_151_out, and_152_out, and_153_out, and_154_out, and_155_out, and_156_out, and_157_out,
       and_158_out, and_159_out, and_160_out, and_161_out, and_162_out, and_163_out, and_164_out,
       and_165_out, and_166_out, and_167_out, and_168_out, and_169_out, and_170_out, and_171_out,
       and_172_out, and_173_out, and_174_out, and_175_out, and_176_out, and_177_out, and_178_out,
       and_179_out, and_180_out, and_181_out, and_182_out, and_183_out, and_184_out, and_185_out,
       and_186_out, and_187_out, and_188_out, clk, clock_1_out, d_ff_1_q, d_ff_2_q, d_ff_3_q, d_ff_4_q,
       d_ff_5_q, d_ff_6_q, d_ff_7_q, d_ff_8_q, d_ff_9_q, d_ff_10_q, d_ff_11_q, d_ff_12_q, d_ff_13_q,
       d_ff_14_q, d_ff_15_q, d_ff_16_q, d_ff_17_q, d_ff_18_q, d_ff_19_q, d_ff_20_q, d_ff_21_q, d_ff_22_q,
       d_ff_23_q, d_ff_24_q, d_ff_25_q, d_ff_26_q, d_ff_27_q, d_ff_28_q, d_ff_29_q, d_ff_30_q, d_ff_31_q,
       d_ff_32_q, d_ff_33_q, d_ff_34_q, d_ff_35_q, d_ff_36_q, d_ff_37_q, d_ff_38_q, d_ff_39_q, d_ff_40_q,
       d_ff_41_q, d_ff_44_q, d_ff_44_qn, d_ff_45_q, d_ff_46_q, d_ff_47_q, d_ff_48_q, d_ff_49_q, d_ff_50_q,
       d_ff_51_q, d_ff_52_q, d_ff_53_q, d_ff_54_q, d_ff_55_q, d_ff_56_q, d_ff_57_q, d_ff_58_q, d_ff_59_q,
       d_ff_60_q, d_ff_61_q, d_ff_62_q, d_ff_63_q, d_ff_64_q, d_ff_65_q, d_ff_66_q, d_ff_67_q, d_ff_68_q,
       d_ff_69_q, d_ff_70_q, d_ff_71_q, d_ff_72_q, d_ff_73_q, d_ff_74_q, d_ff_75_q, data_address,
       data_input_0, data_input_1, data_input_2, data_input_3, data_output_0, data_output_1, data_output_2,
       data_output_3, datamode, fetch_out, halt, Halt_out, load, LOAD_TICK_1, LOAD_TICK_2, LOAD_TICK_3,
       LOAD_TICK_4, not_1_out, not_2_out, not_3_out, not_4_out, not_5_out, not_6_out, not_7_out, not_8_out,
       not_9_out, not_10_out, not_11_out, not_12_out, not_13_out, not_14_out, not_15_out, not_16_out,
       not_17_out, not_18_out, not_19_out, not_21_out, not_22_out, not_23_out, not_24_out, not_25_out,
       not_26_out, not_27_out, not_28_out, not_29_out, not_30_out, not_31_out, not_32_out, not_33_out,
       not_34_out, not_35_out, not_36_out, not_37_out, not_40_out, not_41_out, not_42_out, not_43_out,
       not_44_out, not_45_out, not_46_out, not_47_out, not_48_out, not_49_out, not_50_out, or_1_out,
       or_2_out, or_3_out, or_4_out, or_5_out, or_6_out, or_7_out, or_8_out, or_9_out, or_10_out, or_11_out,
       or_12_out, or_13_out, or_17_out, or_18_out, or_20_out, or_21_out, or_24_out, register_address,
       register_address_LOAD_SAVE, register_input_0_LOAD_SAVE, register_input_1_LOAD_SAVE,
       register_input_2_LOAD_SAVE, register_input_3_LOAD_SAVE, register_mode, register_mode_LOAD_SAVE,
       register_output_0, register_output_1, register_output_2, register_output_3, save, SAVE_TICK_1,
       SAVE_TICK_2, SAVE_TICK_3, SAVE_TICK_4, sub, SUB_TICK_1, SUB_TICK_2, SUB_TICK_3, SUB_TICK_4;

  ALU alu_1 (
    .L2(d_ff_1_q), .L3(d_ff_2_q), .L4(d_ff_3_q), .R4(or_1_out), .clk(clk), .AOUT2(alu_1_aout2),
    .AOUT3(alu_1_aout3), .AOUT4(alu_1_aout4));  // open: L1, R1, R2, R3, cmd, Zero, Negative, Overflow, SignedOverflow, AOUT1
  or or_1 (or_1_out, ADD_TICK_3, LOAD_TICK_3, SAVE_TICK_3, SUB_TICK_3);
  D_Flip_Flop #(.trigger("falling")) d_ff_1 (.D(alu_1_aout2), .clk(clk), .Q(d_ff_1_q));  // open: Qn, preset, reset
  D_Flip_Flop #(.trigger("falling")) d_ff_2 (.D(alu_1_aout3), .clk(clk), .Q(d_ff_2_q));  // open: Qn, preset, reset
  D_Flip_Flop #(.trigger("falling")) d_ff_3 (.D(alu_1_aout4), .clk(clk), .Q(d_ff_3_q));  // open: Qn, preset, reset
  not not_1 (not_1_out, d_ff_3_q);
  not not_2 (not_2_out, d_ff_2_q);
  not not_3 (not_3_out, d_ff_2_q);
  not not_4 (not_4_out, d_ff_3_q);
  not not_5 (not_5_out, d_ff_1_q);
  not not_6 (not_6_out, d_ff_1_q);
  not not_7 (not_7_out, d_ff_3_q);
  not not_8 (not_8_out, d_ff_1_q);
  not not_9 (not_9_out, d_ff_2_q);
  not not_10 (not_10_out, d_ff_1_q);
  not not_11 (not_11_out, d_ff_2_q);
  not not_12 (not_12_out, d_ff_3_q);
  and and_1 (and_1_out, d_ff_1_q, d_ff_2_q, clk, d_ff_3_q);
  and and_2 (and_2_out, and_1_out, not_14_out);
  and and_3 (and_3_out, d_ff_1_q, d_ff_2_q, clk, not_1_out);
  and and_4 (and_4_out, and_3_out, not_14_out);
  and and_5 (and_5_out, d_ff_1_q, not_2_out, clk, d_ff_3_q);
  and and_6 (and_6_out, and_5_out, not_14_out);
  and and_7 (and_7_out, d_ff_1_q, not_3_out, clk, not_4_out);
  and and_8 (and_8_out, and_7_out, not_14_out);
  and and_9 (and_9_out, not_5_out, d_ff_2_q, clk, d_ff_3_q);
  and and_10 (and_10_out, and_9_out, not_14_out);
  and and_11 (and_11_out, not_6_out, d_ff_2_q, clk, not_7_out);
  and and_12 (and_12_out, and_11_out, not_14_out);
  and and_13 (and_13_out, not_8_out, not_9_out, clk, d_ff_3_q);
  and and_14 (and_14_out, and_13_out, not_14_out);
  and and_15 (and_15_out, not_10_out, not_11_out, clk, not_12_out);
  and and_16 (and_16_out, and_15_out, not_14_out);
  not not_13 (not_13_out, in_5);
  not not_14 (not_14_out, not_13_out);
  and and_17 (and_17_out, and_1_out, not_14_out, d_ff_12_q);
  D_Flip_Flop #(.trigger("high")) d_ff_4 (.D(and_17_out), .clk(and_2_out), .Q(d_ff_4_q));  // open: Qn, preset, reset
  and and_18 (and_18_out, and_3_out, not_14_out, d_ff_12_q);
  D_Flip_Flop #(.trigger("high")) d_ff_5 (.D(and_18_out), .clk(and_4_out), .Q(d_ff_5_q));  // open: Qn, preset, reset
  and and_19 (and_19_out, and_5_out, not_14_out, d_ff_12_q);
  D_Flip_Flop #(.trigger("high")) d_ff_6 (.D(and_19_out), .clk(and_6_out), .Q(d_ff_6_q));  // open: Qn, preset, reset
  and and_20 (and_20_out, and_7_out, not_14_out, d_ff_12_q);
  D_Flip_Flop #(.trigger("high")) d_ff_7 (.D(and_20_out), .clk(and_8_out), .Q(d_ff_7_q));  // open: Qn, preset, reset
  and and_21 (and_21_out, and_9_out, not_14_out, d_ff_12_q);
  D_Flip_Flop #(.trigger("high")) d_ff_8 (.D(and_21_out), .clk(and_10_out), .Q(d_ff_8_q));  // open: Qn, preset, reset
  and and_22 (and_22_out, and_11_out, not_14_out, d_ff_12_q);
  D_Flip_Flop #(.trigger("high")) d_ff_9 (.D(and_22_out), .clk(and_12_out), .Q(d_ff_9_q));  // open: Qn, preset, reset
  and and_23 (and_23_out, and_13_out, not_14_out, d_ff_12_q);
  D_Flip_Flop #(.trigger("high")) d_ff_10 (.D(and_23_out), .clk(and_14_out), .Q(d_ff_10_q));  // open: Qn, preset, reset
  and and_24 (and_24_out, and_15_out, not_14_out, d_ff_12_q);
  D_Flip_Flop #(.trigger("high")) d_ff_11 (.D(and_24_out), .clk(and_16_out), .Q(d_ff_11_q));  // open: Qn, preset, reset
  D_Flip_Flop #(.trigger("falling")) d_ff_12 (.D(DataInput1), .clk(clk), .Q(d_ff_12_q));  // open: Qn, preset, reset
  or or_2 (or_2_out, and_25_out, and_26_out, and_27_out, and_28_out, and_29_out, and_30_out, and_31_out, and_32_out);
  and and_25 (and_25_out, d_ff_4_q, and_1_out, not_13_out);
  and and_26 (and_26_out, d_ff_5_q, and_3_out, not_13_out);
  and and_27 (and_27_out, d_ff_6_q, and_5_out, not_13_out);
  and and_28 (and_28_out, d_ff_7_q, and_7_out, not_13_out);
  and and_29 (and_29_out, d_ff_8_q, and_9_out, not_13_out);
  and and_30 (and_30_out, d_ff_9_q, and_11_out, not_13_out);
  and and_31 (and_31_out, d_ff_10_q, and_13_out, not_13_out);
  and and_32 (and_32_out, d_ff_11_q, and_15_out, not_13_out);
  D_Flip_Flop #(.trigger("falling")) d_ff_13 (.D(DataInput2), .clk(clk), .Q(d_ff_13_q));  // open: Qn, preset, reset
  and and_33 (and_33_out, and_1_out, not_14_out, d_ff_13_q);
  D_Flip_Flop #(.trigger("high")) d_ff_14 (.D(and_33_out), .clk(and_2_out), .Q(d_ff_14_q));  // open: Qn, preset, reset
  and and_34 (and_34_out, and_3_out, not_14_out, d_ff_13_q);
  D_Flip_Flop #(.trigger("high")) d_ff_15 (.D(and_34_out), .clk(and_4_out), .Q(d_ff_15_q));  // open: Qn, preset, reset
  and and_35 (and_35_out, and_5_out, not_14_out, d_ff_13_q);
  D_Flip_Flop #(.trigger("high")) d_ff_16 (.D(and_35_out), .clk(and_6_out), .Q(d_ff_16_q));  // open: Qn, preset, reset
  and and_36 (and_36_out, and_7_out, not_14_out, d_ff_13_q);
  D_Flip_Flop #(.trigger("high")) d_ff_17 (.D(and_36_out), .clk(and_8_out), .Q(d_ff_17_q));  // open: Qn, preset, reset
  and and_37 (and_37_out, and_9_out, not_14_out, d_ff_13_q);
  D_Flip_Flop #(.trigger("high")) d_ff_18 (.D(and_37_out), .clk(and_10_out), .Q(d_ff_18_q));  // open: Qn, preset, reset
  and and_38 (and_38_out, and_11_out, not_14_out, d_ff_13_q);
  D_Flip_Flop #(.trigger("high")) d_ff_19 (.D(and_38_out), .clk(and_12_out), .Q(d_ff_19_q));  // open: Qn, preset, reset
  and and_39 (and_39_out, and_13_out, not_14_out, d_ff_13_q);
  D_Flip_Flop #(.trigger("high")) d_ff_20 (.D(and_39_out), .clk(and_14_out), .Q(d_ff_20_q));  // open: Qn, preset, reset
  and and_40 (and_40_out, and_15_out, not_14_out, d_ff_13_q);
  D_Flip_Flop #(.trigger("high")) d_ff_21 (.D(and_40_out), .clk(and_16_out), .Q(d_ff_21_q));  // open: Qn, preset, reset
  D_Flip_Flop #(.trigger("falling")) d_ff_22 (.D(DataInput3), .clk(clk), .Q(d_ff_22_q));  // open: Qn, preset, reset
  or or_3 (or_3_out, and_41_out, and_42_out, and_43_out, and_44_out, and_45_out, and_46_out, and_47_out, and_48_out);
  and and_41 (and_41_out, d_ff_14_q, and_1_out, not_13_out);
  and and_42 (and_42_out, d_ff_15_q, and_3_out, not_13_out);
  and and_43 (and_43_out, d_ff_16_q, and_5_out, not_13_out);
  and and_44 (and_44_out, d_ff_17_q, and_7_out, not_13_out);
  and and_45 (and_45_out, d_ff_18_q, and_9_out, not_13_out);
  and and_46 (and_46_out, d_ff_19_q, and_11_out, not_13_out);
  and and_47 (and_47_out, d_ff_20_q, and_13_out, not_13_out);
  and and_48 (and_48_out, d_ff_21_q, and_15_out, not_13_out);
  D_Flip_Flop #(.trigger("falling")) d_ff_23 (.D(DataInput4), .clk(clk), .Q(d_ff_23_q));  // open: Qn, preset, reset
  and and_49 (and_49_out, and_1_out, not_14_out, d_ff_22_q);
  D_Flip_Flop #(.trigger("high")) d_ff_24 (.D(and_49_out), .clk(and_2_out), .Q(d_ff_24_q));  // open: Qn, preset, reset
  and and_50 (and_50_out, and_3_out, not_14_out, d_ff_22_q);
  D_Flip_Flop #(.trigger("high")) d_ff_25 (.D(and_50_out), .clk(and_4_out), .Q(d_ff_25_q));  // open: Qn, preset, reset
  and and_51 (and_51_out, and_5_out, not_14_out, d_ff_22_q);
  D_Flip_Flop #(.trigger("high")) d_ff_26 (.D(and_51_out), .clk(and_6_out), .Q(d_ff_26_q));  // open: Qn, preset, reset
  and and_52 (and_52_out, and_7_out, not_14_out, d_ff_22_q);
  D_Flip_Flop #(.trigger("high")) d_ff_27 (.D(and_52_out), .clk(and_8_out), .Q(d_ff_27_q));  // open: Qn, preset, reset
  and and_53 (and_53_out, and_9_out, not_14_out, d_ff_22_q);
  D_Flip_Flop #(.trigger("high")) d_ff_28 (.D(and_53_out), .clk(and_10_out), .Q(d_ff_28_q));  // open: Qn, preset, reset
  and and_54 (and_54_out, and_11_out, not_14_out, d_ff_22_q);
  D_Flip_Flop #(.trigger("high")) d_ff_29 (.D(and_54_out), .clk(and_12_out), .Q(d_ff_29_q));  // open: Qn, preset, reset
  and and_55 (and_55_out, and_13_out, not_14_out, d_ff_22_q);
  D_Flip_Flop #(.trigger("high")) d_ff_30 (.D(and_55_out), .clk(and_14_out), .Q(d_ff_30_q));  // open: Qn, preset, reset
  and and_56 (and_56_out, and_15_out, not_14_out, d_ff_22_q);
  D_Flip_Flop #(.trigger("high")) d_ff_31 (.D(and_56_out), .clk(and_16_out), .Q(d_ff_31_q));  // open: Qn, preset, reset
  or or_4 (or_4_out, and_57_out, and_58_out, and_59_out, and_60_out, and_61_out, and_62_out, and_63_out, and_64_out);
  and and_57 (and_57_out, and_1_out, d_ff_24_q, not_13_out);
  and and_58 (and_58_out, d_ff_25_q, and_3_out, not_13_out);
  and and_59 (and_59_out, d_ff_26_q, and_5_out, not_13_out);
  and and_60 (and_60_out, d_ff_27_q, and_7_out, not_13_out);
  and and_61 (and_61_out, d_ff_28_q, and_9_out, not_13_out);
  and and_62 (and_62_out, d_ff_29_q, and_11_out, not_13_out);
  and and_63 (and_63_out, d_ff_30_q, and_13_out, not_13_out);
  and and_64 (and_64_out, d_ff_31_q, and_15_out, not_13_out);
  and and_65 (and_65_out, and_1_out, not_14_out, d_ff_23_q);
  D_Flip_Flop #(.trigger("high")) d_ff_32 (.D(and_65_out), .clk(and_2_out), .Q(d_ff_32_q));  // open: Qn, preset, reset
  and and_66 (and_66_out, and_3_out, not_14_out, d_ff_23_q);
  D_Flip_Flop #(.trigger("high")) d_ff_33 (.D(and_66_out), .clk(and_4_out), .Q(d_ff_33_q));  // open: Qn, preset, reset
  and and_67 (and_67_out, and_5_out, not_14_out, d_ff_23_q);
  D_Flip_Flop #(.trigger("high")) d_ff_34 (.D(and_67_out), .clk(and_6_out), .Q(d_ff_34_q));  // open: Qn, preset, reset
  and and_68 (and_68_out, and_7_out, not_14_out, d_ff_23_q);
  D_Flip_Flop #(.trigger("high")) d_ff_35 (.D(and_68_out), .clk(and_8_out), .Q(d_ff_35_q));  // open: Qn, preset, reset
  and and_69 (and_69_out, and_9_out, not_14_out, d_ff_23_q);
  D_Flip_Flop #(.trigger("high")) d_ff_36 (.D(and_69_out), .clk(and_10_out), .Q(d_ff_36_q));  // open: Qn, preset, reset
  and and_70 (and_70_out, and_11_out, not_14_out, d_ff_23_q);
  D_Flip_Flop #(.trigger("high")) d_ff_37 (.D(and_70_out), .clk(and_12_out), .Q(d_ff_37_q));  // open: Qn, preset, reset
  and and_71 (and_71_out, and_13_out, not_14_out, d_ff_23_q);
  D_Flip_Flop #(.trigger("high")) d_ff_38 (.D(and_71_out), .clk(and_14_out), .Q(d_ff_38_q));  // open: Qn, preset, reset
  and and_72 (and_72_out, and_15_out, not_14_out, d_ff_23_q);
  D_Flip_Flop #(.trigger("high")) d_ff_39 (.D(and_72_out), .clk(and_16_out), .Q(d_ff_39_q));  // open: Qn, preset, reset
  or or_5 (or_5_out, and_73_out, and_74_out, and_75_out, and_76_out, and_77_out, and_78_out, and_79_out, and_80_out);
  and and_73 (and_73_out, d_ff_32_q, and_1_out, not_13_out);
  and and_74 (and_74_out, d_ff_33_q, and_3_out, not_13_out);
  and and_75 (and_75_out, d_ff_34_q, and_5_out, not_13_out);
  and and_76 (and_76_out, d_ff_35_q, and_7_out, not_13_out);
  and and_77 (and_77_out, d_ff_36_q, and_9_out, not_13_out);
  and and_78 (and_78_out, d_ff_37_q, and_11_out, not_13_out);
  and and_79 (and_79_out, d_ff_38_q, and_13_out, not_13_out);
  and and_80 (and_80_out, d_ff_39_q, and_15_out, not_13_out);
  D_Flip_Flop #(.trigger("falling")) d_ff_40 (.D(or_2_out), .clk(clk), .Q(d_ff_40_q));  // open: Qn, preset, reset
  D_Flip_Flop #(.trigger("falling")) d_ff_41 (.D(or_3_out), .clk(clk), .Q(d_ff_41_q));  // open: Qn, preset, reset
  D_Flip_Flop #(.trigger("falling")) d_ff_42 (
    .D(or_4_out), .clk(clk), .Q(register_address_LOAD_SAVE));  // open: Qn, preset, reset
  D_Flip_Flop #(.trigger("falling")) d_ff_43 (.D(or_5_out), .clk(clk), .Q(data_address));  // open: Qn, preset, reset
  and and_81 (and_81_out, register_address_LOAD_SAVE, data_address);
  not not_15 (not_15_out, d_ff_40_q);
  not not_16 (not_16_out, d_ff_41_q);
  not not_17 (not_17_out, d_ff_40_q);
  not not_18 (not_18_out, d_ff_41_q);
  not not_19 (not_19_out, and_81_out);
  D_Flip_Flop #(.trigger("falling")) d_ff_44 (
    .D(d_ff_44_qn), .clk(clk), .Q(d_ff_44_q), .Qn(d_ff_44_qn));  // open: preset, reset
  and u_Load (load, not_15_out, not_16_out);
  and u_Save (save, not_17_out, d_ff_41_q);
  and u_Add (add, d_ff_40_q, not_18_out);
  and u_Sub (sub, d_ff_40_q, not_19_out, d_ff_41_q);
  and u_Halt (Halt_out, d_ff_41_q, and_81_out, d_ff_40_q);
  not not_20 (halt, Halt_out);
  or or_6 (or_6_out, and_82_out, and_83_out);
  and and_82 (and_82_out, d_ff_45_q, not_21_out);
  and and_83 (and_83_out, d_ff_44_q, d_ff_44_q);
  not not_21 (not_21_out, d_ff_44_q);
  D_Flip_Flop #(.trigger("falling")) d_ff_45 (.D(or_6_out), .clk(clk), .Q(d_ff_45_q));  // open: Qn, preset, reset
  and fetch (fetch_out, d_ff_45_q, load);
  and and_84 (add_or_sub_instr, d_ff_40_q, d_ff_41_q);
  D_Flip_Flop #(.trigger("falling")) d_ff_46 (.D(alu_2_aout3), .clk(clk), .Q(d_ff_46_q));  // open: Qn, preset, reset
  D_Flip_Flop #(.trigger("falling")) d_ff_47 (.D(alu_2_aout4), .clk(clk), .Q(d_ff_47_q));  // open: Qn, preset, reset
  not not_22 (not_22_out, d_ff_46_q);
  not not_23 (not_23_out, d_ff_47_q);
  not not_24 (not_24_out, d_ff_46_q);
  not not_25 (not_25_out, d_ff_47_q);
  not not_26 (not_26_out, d_ff_46_q);
  not not_27 (not_27_out, d_ff_47_q);
  not not_28 (not_28_out, d_ff_46_q);
  not not_29 (not_29_out, d_ff_47_q);
  not not_30 (not_30_out, d_ff_46_q);
  not not_31 (not_31_out, d_ff_47_q);
  not not_32 (not_32_out, d_ff_46_q);
  not not_33 (not_33_out, d_ff_47_q);
  not not_34 (not_34_out, d_ff_46_q);
  not not_35 (not_35_out, d_ff_47_q);
  not not_36 (not_36_out, d_ff_46_q);
  not not_37 (not_37_out, d_ff_47_q);
  ALU alu_2 (
    .L4(or_7_out), .R3(d_ff_46_q), .R4(d_ff_47_q), .clk(clk), .AOUT3(alu_2_aout3), .AOUT4(alu_2_aout4));  // open: L1, L2, L3, R1, R2, cmd, Zero, Negative, Overflow, SignedOverflow, AOUT1, AOUT2
  or or_7 (or_7_out, LOAD_TICK_4, LOAD_TICK_3, ADD_TICK_1, ADD_TICK_2, ADD_TICK_3, ADD_TICK_4, SAVE_TICK_1, SAVE_TICK_2, LOAD_TICK_1, LOAD_TICK_2, SUB_TICK_1, SUB_TICK_2, SUB_TICK_3, SUB_TICK_4, SAVE_TICK_3, SAVE_TICK_4);
  and and_85 (LOAD_TICK_1, not_22_out, fetch_out, not_23_out);
  and and_86 (LOAD_TICK_2, not_24_out, fetch_out, d_ff_47_q);
  and and_87 (LOAD_TICK_3, d_ff_46_q, fetch_out, not_25_out);
  and and_88 (LOAD_TICK_4, d_ff_46_q, fetch_out, d_ff_47_q);
  and and_89 (SAVE_TICK_1, not_26_out, save, not_27_out);
  and and_90 (SAVE_TICK_2, not_28_out, save, d_ff_47_q);
  and and_91 (SAVE_TICK_3, d_ff_46_q, save, not_29_out);
  and and_92 (SAVE_TICK_4, d_ff_46_q, save, d_ff_47_q);
  and and_93 (ADD_TICK_1, not_30_out, add, not_31_out);
  and and_94 (ADD_TICK_2, not_32_out, add, d_ff_47_q);
  and and_95 (ADD_TICK_3, d_ff_46_q, add, not_33_out);
  and and_96 (ADD_TICK_4, d_ff_46_q, add, d_ff_47_q);
  and and_97 (SUB_TICK_1, not_34_out, sub, not_35_out);
  and and_98 (SUB_TICK_2, not_36_out, sub, d_ff_47_q);
  and and_99 (SUB_TICK_3, d_ff_46_q, sub, not_37_out);
  and and_100 (SUB_TICK_4, d_ff_46_q, sub, d_ff_47_q);
  and and_101 (register_input_0_LOAD_SAVE, data_output_0, fetch_out);
  and and_102 (register_input_1_LOAD_SAVE, data_output_1, fetch_out);
  and and_103 (register_input_2_LOAD_SAVE, data_output_2, fetch_out);
  and and_104 (register_input_3_LOAD_SAVE, data_output_3, fetch_out);
  and and_105 (data_input_0, register_output_0, save);
  and and_106 (data_input_1, register_output_1, save);
  and and_107 (data_input_2, register_output_2, save);
  and and_108 (data_input_3, register_output_3, save);
  not not_38 (datamode, save);
  or or_8 (or_8_out, ADD_TICK_1, SUB_TICK_1);
  or or_9 (or_9_out, ADD_TICK_2, SUB_TICK_2);
  and and_109 (clk, halt, clock_1_out);
  Clock clock_1 (.out(clock_1_out));
  not not_39 (register_mode_LOAD_SAVE, fetch_out);
  or or_10 (or_10_out, ADD_TICK_3, SUB_TICK_3);
  or or_11 (or_11_out, ADD_TICK_4, SUB_TICK_4);
  or or_12 (or_12_out, or_10_out, or_11_out);
  and and_110 (and_110_out, register_address_LOAD_SAVE, or_8_out);
  and and_111 (and_111_out, or_9_out, data_address);
  and and_112 (and_112_out, register_address_LOAD_SAVE, or_12_out);
  not not_40 (not_40_out, or_11_out);
  or or_13 (or_13_out, and_110_out, and_111_out, and_112_out);
  or or_14 (register_address, and_113_out, and_114_out);
  and and_113 (and_113_out, register_address_LOAD_SAVE, or_24_out);
  and and_114 (and_114_out, not_41_out, or_13_out);
  not not_41 (not_41_out, or_24_out);
  not not_42 (not_42_out, register_address);
  and and_115 (and_115_out, clk, register_address);
  and and_116 (and_116_out, clk, not_42_out);
  or or_15 (register_mode, and_117_out, and_118_out);
  and and_117 (and_117_out, register_mode_LOAD_SAVE, or_24_out);
  and and_118 (and_118_out, not_43_out, not_40_out);
  not not_43 (not_43_out, or_24_out);
  and and_119 (and_119_out, and_115_out, not_44_out);
  and and_120 (and_120_out, and_116_out, not_44_out);
  not not_44 (not_44_out, register_mode);
  and and_121 (and_121_out, and_115_out, not_44_out, d_ff_50_q);
  D_Flip_Flop #(.trigger("high")) d_ff_48 (
    .D(and_121_out), .clk(and_119_out), .Q(d_ff_48_q));  // open: Qn, preset, reset
  and and_122 (and_122_out, and_116_out, not_44_out, d_ff_50_q);
  D_Flip_Flop #(.trigger("high")) d_ff_49 (
    .D(and_122_out), .clk(and_120_out), .Q(d_ff_49_q));  // open: Qn, preset, reset
  or or_16 (register_output_3, and_123_out, and_124_out);
  and and_123 (and_123_out, d_ff_48_q, and_115_out, register_mode);
  and and_124 (and_124_out, d_ff_49_q, and_116_out, register_mode);
  D_Flip_Flop #(.trigger("falling")) d_ff_50 (.D(or_17_out), .clk(clk), .Q(d_ff_50_q));  // open: Qn, preset, reset
  or or_17 (or_17_out, and_125_out, and_126_out);
  and and_125 (and_125_out, ALU_output_3, not_45_out);
  and and_126 (and_126_out, or_24_out, register_input_3_LOAD_SAVE);
  not not_45 (not_45_out, or_24_out);
  D_Flip_Flop #(.trigger("falling")) d_ff_51 (.D(or_18_out), .clk(clk), .Q(d_ff_51_q));  // open: Qn, preset, reset
  or or_18 (or_18_out, and_127_out, and_128_out);
  and and_127 (and_127_out, ALU_output_2, not_46_out);
  and and_128 (and_128_out, or_24_out, register_input_2_LOAD_SAVE);
  not not_46 (not_46_out, or_24_out);
  or or_19 (register_output_2, and_133_out, and_134_out);
  and and_129 (and_129_out, and_115_out, not_44_out, d_ff_51_q);
  and and_130 (and_130_out, and_116_out, not_44_out, d_ff_51_q);
  D_Flip_Flop #(.trigger("falling")) d_ff_52 (.D(or_20_out), .clk(clk), .Q(d_ff_52_q));  // open: Qn, preset, reset
  or or_20 (or_20_out, and_131_out, and_132_out);
  and and_131 (and_131_out, ALU_output_1, not_47_out);
  and and_132 (and_132_out, or_24_out, register_input_1_LOAD_SAVE);
  not not_47 (not_47_out, or_24_out);
  and and_133 (and_133_out, d_ff_53_q, and_115_out, register_mode);
  D_Flip_Flop #(.trigger("high")) d_ff_53 (
    .D(and_129_out), .clk(and_119_out), .Q(d_ff_53_q));  // open: Qn, preset, reset
  and and_134 (and_134_out, d_ff_54_q, and_116_out, register_mode);
  D_Flip_Flop #(.trigger("high")) d_ff_54 (
    .D(and_130_out), .clk(and_120_out), .Q(d_ff_54_q));  // open: Qn, preset, reset
  D_Flip_Flop #(.trigger("falling")) d_ff_55 (.D(or_21_out), .clk(clk), .Q(d_ff_55_q));  // open: Qn, preset, reset
  or or_21 (or_21_out, and_135_out, and_136_out);
  and and_135 (and_135_out, ALU_output_0, not_48_out);
  and and_136 (and_136_out, or_24_out, register_input_0_LOAD_SAVE);
  not not_48 (not_48_out, or_24_out);
  or or_22 (register_output_1, and_139_out, and_140_out);
  or or_23 (register_output_0, and_159_out, and_160_out);
  and and_137 (and_137_out, and_115_out, not_44_out, d_ff_52_q);
  D_Flip_Flop #(.trigger("high")) d_ff_56 (
    .D(and_137_out), .clk(and_119_out), .Q(d_ff_56_q));  // open: Qn, preset, reset
  and and_138 (and_138_out, and_116_out, not_44_out, d_ff_52_q);
  D_Flip_Flop #(.trigger("high")) d_ff_57 (
    .D(and_138_out), .clk(and_120_out), .Q(d_ff_57_q));  // open: Qn, preset, reset
  or or_24 (or_24_out, load, save);
  and and_139 (and_139_out, d_ff_56_q, and_115_out, register_mode);
  and and_140 (and_140_out, d_ff_57_q, and_116_out, register_mode);
  and and_141 (and_141_out, and_115_out, not_44_out, d_ff_55_q);
  D_Flip_Flop #(.trigger("high")) d_ff_58 (
    .D(and_141_out), .clk(and_119_out), .Q(d_ff_58_q));  // open: Qn, preset, reset
  and and_142 (and_142_out, and_116_out, not_44_out, d_ff_55_q);
  D_Flip_Flop #(.trigger("high")) d_ff_59 (
    .D(and_142_out), .clk(and_120_out), .Q(d_ff_59_q));  // open: Qn, preset, reset
  D_Flip_Flop #(.trigger("high")) d_ff_60 (
    .D(and_143_out), .clk(and_144_out), .Q(d_ff_60_q));  // open: Qn, preset, reset
  and and_143 (and_143_out, register_output_3, or_8_out);
  and and_144 (and_144_out, or_8_out, clk);
  D_Flip_Flop #(.trigger("high")) d_ff_61 (
    .D(and_145_out), .clk(and_146_out), .Q(d_ff_61_q));  // open: Qn, preset, reset
  and and_145 (and_145_out, register_output_2, or_8_out);
  and and_146 (and_146_out, or_8_out, clk);
  D_Flip_Flop #(.trigger("high")) d_ff_62 (
    .D(and_147_out), .clk(and_148_out), .Q(d_ff_62_q));  // open: Qn, preset, reset
  and and_147 (and_147_out, register_output_1, or_8_out);
  and and_148 (and_148_out, or_8_out, clk);
  D_Flip_Flop #(.trigger("high")) d_ff_63 (
    .D(and_149_out), .clk(and_150_out), .Q(d_ff_63_q));  // open: Qn, preset, reset
  and and_149 (and_149_out, register_output_0, or_8_out);
  and and_150 (and_150_out, or_8_out, clk);
  D_Flip_Flop #(.trigger("high")) d_ff_64 (
    .D(and_151_out), .clk(and_152_out), .Q(d_ff_64_q));  // open: Qn, preset, reset
  and and_151 (and_151_out, register_output_3, or_9_out);
  and and_152 (and_152_out, or_9_out, clk);
  D_Flip_Flop #(.trigger("high")) d_ff_65 (
    .D(and_153_out), .clk(and_154_out), .Q(d_ff_65_q));  // open: Qn, preset, reset
  and and_153 (and_153_out, register_output_2, or_9_out);
  and and_154 (and_154_out, or_9_out, clk);
  D_Flip_Flop #(.trigger("high")) d_ff_66 (
    .D(and_155_out), .clk(and_156_out), .Q(d_ff_66_q));  // open: Qn, preset, reset
  and and_155 (and_155_out, register_output_1, or_9_out);
  and and_156 (and_156_out, or_9_out, clk);
  D_Flip_Flop #(.trigger("high")) d_ff_67 (
    .D(and_157_out), .clk(and_158_out), .Q(d_ff_67_q));  // open: Qn, preset, reset
  and and_157 (and_157_out, register_output_0, or_9_out);
  and and_158 (and_158_out, or_9_out, clk);
  and and_159 (and_159_out, d_ff_58_q, and_115_out, register_mode);
  and and_160 (and_160_out, d_ff_59_q, and_116_out, register_mode);
  and and_161 (and_161_out, d_ff_60_q, or_10_out);
  and and_162 (and_162_out, d_ff_61_q, or_10_out);
  and and_163 (and_163_out, d_ff_62_q, or_10_out);
  and and_164 (and_164_out, d_ff_63_q, or_10_out);
  and and_165 (and_165_out, d_ff_64_q, or_10_out);
  and and_166 (and_166_out, d_ff_65_q, or_10_out);
  and and_167 (and_167_out, d_ff_66_q, or_10_out);
  and and_168 (and_168_out, d_ff_67_q, or_10_out);
  ALU alu_3 (
    .L1(and_161_out), .L2(and_162_out), .L3(and_163_out), .L4(and_164_out), .R1(and_165_out),
    .R2(and_166_out), .R3(and_167_out), .R4(and_168_out), .clk(clk), .cmd(add_or_sub_instr), .Zero(out_6),
    .Negative(out_7), .Overflow(out_8), .SignedOverflow(out_9), .AOUT1(ALU_output_3), .AOUT2(ALU_output_2),
    .AOUT3(ALU_output_1), .AOUT4(ALU_output_0));
  not not_49 (not_49_out, data_address);
  and and_169 (and_169_out, clk, data_address);
  and and_170 (and_170_out, clk, not_49_out);
  and and_171 (and_171_out, and_169_out, not_50_out);
  and and_172 (and_172_out, and_170_out, not_50_out);
  not not_50 (not_50_out, datamode);
  and and_173 (and_173_out, and_169_out, not_50_out, data_input_3);
  D_Flip_Flop #(.trigger("high")) d_ff_68 (
    .D(and_173_out), .clk(and_171_out), .Q(d_ff_68_q));  // open: Qn, preset, reset
  and and_174 (and_174_out, and_170_out, not_50_out, data_input_3);
  D_Flip_Flop #(.trigger("high")) d_ff_69 (
    .D(and_174_out), .clk(and_172_out), .Q(d_ff_69_q));  // open: Qn, preset, reset
  and and_175 (and_175_out, d_ff_68_q, and_169_out, datamode);
  and and_176 (and_176_out, d_ff_69_q, and_170_out, datamode);
  or or_25 (data_output_3, and_175_out, and_176_out);
  and and_177 (and_177_out, and_169_out, not_50_out, data_input_2);
  D_Flip_Flop #(.trigger("high")) d_ff_70 (
    .D(and_177_out), .clk(and_171_out), .Q(d_ff_70_q));  // open: Qn, preset, reset
  and and_178 (and_178_out, and_170_out, not_50_out, data_input_2);
  D_Flip_Flop #(.trigger("high")) d_ff_71 (
    .D(and_178_out), .clk(and_172_out), .Q(d_ff_71_q));  // open: Qn, preset, reset
  or or_26 (data_output_2, and_179_out, and_180_out);
  and and_179 (and_179_out, d_ff_70_q, and_169_out, datamode);
  and and_180 (and_180_out, d_ff_71_q, and_170_out, datamode);
  or or_27 (data_output_1, and_183_out, and_184_out);
  and and_181 (and_181_out, and_169_out, not_50_out, data_input_1);
  D_Flip_Flop #(.trigger("high")) d_ff_72 (
    .D(and_181_out), .clk(and_171_out), .Q(d_ff_72_q));  // open: Qn, preset, reset
  and and_182 (and_182_out, and_170_out, not_50_out, data_input_1);
  D_Flip_Flop #(.trigger("high")) d_ff_73 (
    .D(and_182_out), .clk(and_172_out), .Q(d_ff_73_q));  // open: Qn, preset, reset
  or or_28 (data_output_0, and_187_out, and_188_out);
  and and_183 (and_183_out, d_ff_72_q, and_169_out, datamode);
  and and_184 (and_184_out, d_ff_73_q, and_170_out, datamode);
  and and_185 (and_185_out, and_169_out, not_50_out, data_input_0);
  and and_186 (and_186_out, and_170_out, not_50_out, data_input_0);
  and and_187 (and_187_out, d_ff_74_q, and_169_out, datamode);
  D_Flip_Flop #(.trigger("high")) d_ff_74 (
    .D(and_185_out), .clk(and_171_out), .Q(d_ff_74_q));  // open: Qn, preset, reset
  and and_188 (and_188_out, d_ff_75_q, and_170_out, datamode);
  D_Flip_Flop #(.trigger("high")) d_ff_75 (
    .D(and_186_out), .clk(and_172_out), .Q(d_ff_75_q));  // open: Qn, preset, reset

  // Notes on the sheet:
  //   4 pins always +1
  //   Leticia Huang 261068858
  //   Rayane Bouafia 261119286
  //   PC
  //   Top pin always 0 for cmd
  //   PC address
  //   Mode input pin
  //   INverted: by default 1 to Read from I-RAM
  //   Instruction RAM
  //   IR
  //   INVERTED SO THAT THE REGISTER BLOCK IS IN READ MODE BY DEFAULT
  //   REGISTER BLOCK
  //   MULTIPLEXOR
  //   R1
  //   R0
  //   Need to add this for add/sub, need to specify which register to store to
  //   MULTIPLEXOR 
  //   RIGHT
  //   LEFT
  //   ALU
  //   Status
  //   ADDRESS 1
  //   ADDRESS 0
  //   DATA RAM
endmodule

module ALU (
  input  L1,
  input  L2,
  input  L3,
  input  L4,
  input  R1,
  input  R2,
  input  R3,
  input  R4,
  input  clk,
  input  cmd,
  output Zero,
  output Negative,
  output Overflow,
  output SignedOverflow,
  output AOUT1,
  output AOUT2,
  output AOUT3,
  output AOUT4
);

  wire and_1_out, and_2_out, and_3_out, and_4_out, and_5_out, and_6_out, and_7_out, and_8_out, and_9_out,
       and_10_out, and_11_out, and_12_out, and_13_out, and_14_out, and_15_out, and_16_out, and_17_out,
       and_18_out, and_19_out, and_20_out, and_21_out, and_22_out, and_24_out, and_25_out, and_26_out,
       and_27_out, and_28_out, and_29_out, fulladder_1_c, fulladder_2_c, fulladder_3_c, Neg_out, not_1_out,
       not_2_out, not_3_out, not_4_out, not_5_out, not_6_out, not_7_out, not_8_out, not_9_out, not_10_out,
       not_11_out, not_12_out, not_13_out, not_14_out, not_15_out, not_16_out, not_17_out, not_18_out,
       or_1_out, or_2_out, or_3_out, or_4_out, or_5_out, Pos_out, xor_2_out, xor_3_out, xor_4_out, xor_5_out;

  not not_1 (not_1_out, cmd);
  and and_1 (and_1_out, L1, clk);
  and and_2 (and_2_out, L2, clk);
  and and_3 (and_3_out, L3, clk);
  fullAdder fulladder_1 (.A(or_1_out), .B(and_1_out), .Carry(fulladder_2_c), .C(fulladder_1_c), .Sum(AOUT1));
  and and_4 (and_4_out, L4, clk);
  fullAdder fulladder_2 (.A(or_2_out), .B(and_2_out), .Carry(fulladder_3_c), .C(fulladder_2_c), .Sum(AOUT2));
  or or_1 (or_1_out, xor_2_out, and_6_out);
  fullAdder fulladder_3 (.A(or_3_out), .B(and_3_out), .Carry(and_5_out), .C(fulladder_3_c), .Sum(AOUT3));
  or or_2 (or_2_out, xor_3_out, and_8_out);
  or or_3 (or_3_out, xor_4_out, and_9_out);
  and and_5 (and_5_out, and_4_out, or_4_out);
  xor xor_1 (AOUT4, and_4_out, or_4_out);
  and and_6 (and_6_out, and_12_out, not_1_out);
  and and_7 (and_7_out, not_6_out, and_10_out);
  or or_4 (or_4_out, xor_5_out, and_14_out);
  not not_2 (not_2_out, AOUT4);
  not not_3 (not_3_out, AOUT3);
  not not_4 (not_4_out, AOUT2);
  not not_5 (not_5_out, AOUT1);
  and and_8 (and_8_out, and_13_out, not_1_out);
  and and_9 (and_9_out, and_17_out, not_1_out);
  xor xor_2 (xor_2_out, not_6_out, and_10_out);
  and and_10 (and_10_out, not_10_out, and_16_out);
  and and_11 (and_11_out, not_2_out, not_3_out, not_4_out, not_5_out);
  and and_12 (and_12_out, R1, clk);
  and and_13 (and_13_out, R2, clk);
  and and_14 (and_14_out, and_18_out, not_1_out);
  and and_15 (and_15_out, and_12_out, cmd);
  not not_6 (not_6_out, and_15_out);
  xor xor_3 (xor_3_out, not_10_out, and_16_out);
  and and_16 (and_16_out, not_11_out, and_22_out);
  not not_7 (not_7_out, or_1_out);
  not not_8 (not_8_out, and_1_out);
  not not_9 (not_9_out, or_1_out);
  and and_17 (and_17_out, R3, clk);
  and and_18 (and_18_out, R4, clk);
  and and_19 (and_19_out, and_13_out, cmd);
  and and_20 (and_20_out, and_17_out, cmd);
  and and_21 (and_21_out, and_18_out, cmd);
  not not_10 (not_10_out, and_19_out);
  not not_11 (not_11_out, and_20_out);
  not not_12 (not_12_out, and_21_out);
  xor xor_4 (xor_4_out, not_11_out, and_22_out);
  and and_22 (and_22_out, not_12_out, 1'b1);
  and Neg (Neg_out, or_1_out, and_1_out);
  and Pos (Pos_out, not_7_out, not_8_out);
  and and_23 (Zero, and_11_out, clk);
  xor xor_5 (xor_5_out, not_12_out, 1'b1);
  and and_24 (and_24_out, AOUT1, Neg_out);
  and and_25 (and_25_out, Pos_out, AOUT1);
  and and_26 (and_26_out, not_13_out, not_9_out, fulladder_1_c);
  not not_13 (not_13_out, cmd);
  not not_14 (not_14_out, fulladder_1_c);
  and and_27 (and_27_out, and_24_out, not_14_out);
  or or_5 (or_5_out, and_26_out, and_25_out, and_27_out);
  not not_15 (not_15_out, Zero);
  and notZero (Overflow, or_5_out, not_15_out);
  not not_16 (not_16_out, AOUT1);
  or or_6 (SignedOverflow, and_29_out, and_28_out);
  and and_28 (and_28_out, and_1_out, not_16_out, and_12_out);
  not not_17 (not_17_out, and_12_out);
  and and_29 (and_29_out, not_17_out, AOUT1, not_18_out);
  not not_18 (not_18_out, and_1_out);

  assign Negative = AOUT1;

  // Other names for the same wires on the sheet: Clock = clk

  // Notes on the sheet:
  //   Add/Sub command
  //   0 add, 1 sub
  //   B Input
  //   A-out output
  //   A Input
  //   Adder
  //   2's Complement
  //   Status output
  //   -8 + -8 is underflow (not supported)
endmodule

module fullAdder (
  input  A,
  input  B,
  input  Carry,
  output C,
  output Sum
);

  wire and_1_out, and_2_out, xor_1_out;

  and and_1 (and_1_out, A, B);
  xor xor_1 (xor_1_out, A, B);
  and and_2 (and_2_out, xor_1_out, Carry);
  or or_1 (C, and_1_out, and_2_out);
  xor xor_2 (Sum, xor_1_out, Carry);
endmodule

module Registers (
  input  InstrAddr1,
  input  InstrAddr2,
  input  InstrAddr3,
  input  Mode,
  input  DataInput1,
  input  DataInput2,
  input  DataInput3,
  input  DataInput4,
  output Out1,
  output Out2,
  output Out3,
  output Out4
);

  wire and_1_out, and_2_out, and_3_out, and_4_out, and_5_out, and_6_out, and_7_out, and_8_out, and_9_out,
       and_10_out, and_11_out, and_12_out, and_13_out, and_14_out, and_15_out, and_16_out, and_17_out,
       and_18_out, and_19_out, and_20_out, and_21_out, and_22_out, and_23_out, and_24_out, and_25_out,
       and_26_out, and_27_out, and_28_out, and_29_out, and_30_out, and_31_out, and_32_out, and_33_out,
       and_34_out, and_35_out, and_36_out, and_37_out, and_38_out, and_39_out, and_40_out, and_41_out,
       and_42_out, and_43_out, and_44_out, and_45_out, and_46_out, and_47_out, and_48_out, and_49_out,
       and_50_out, and_51_out, and_52_out, and_53_out, and_54_out, and_55_out, and_56_out, and_57_out,
       and_58_out, and_59_out, and_60_out, and_61_out, and_62_out, and_63_out, and_64_out, and_65_out,
       and_66_out, and_67_out, and_68_out, and_69_out, and_70_out, and_71_out, and_72_out, and_73_out,
       and_74_out, and_75_out, and_76_out, and_77_out, and_78_out, and_79_out, and_80_out, clock_1_out,
       d_ff_1_q, d_ff_2_q, d_ff_3_q, d_ff_4_q, d_ff_5_q, d_ff_6_q, d_ff_7_q, d_ff_8_q, d_ff_9_q, d_ff_10_q,
       d_ff_11_q, d_ff_12_q, d_ff_13_q, d_ff_14_q, d_ff_16_q, d_ff_17_q, d_ff_18_q, d_ff_19_q, d_ff_20_q,
       d_ff_21_q, d_ff_22_q, d_ff_23_q, d_ff_24_q, d_ff_26_q, d_ff_29_q, d_ff_30_q, d_ff_31_q, d_ff_32_q,
       d_ff_33_q, d_ff_34_q, d_ff_35_q, d_ff_36_q, d_ff_37_q, d_ff_38_q, d_ff_39_q, d_ff_40_q, d_ff_41_q,
       d_ff_42_q, d_ff_43_q, d_ff_44_q, not_1_out, not_2_out, not_3_out, not_4_out, not_5_out, not_6_out,
       not_7_out, not_8_out, not_9_out, not_10_out, not_11_out, not_12_out, not_13_out, or_1_out, or_2_out,
       or_3_out, or_4_out;

  D_Flip_Flop #(.trigger("falling")) d_ff_1 (
    .D(InstrAddr1), .clk(clock_1_out), .Q(d_ff_1_q));  // open: Qn, preset, reset
  Clock clock_1 (.out(clock_1_out));
  D_Flip_Flop #(.trigger("falling")) d_ff_2 (
    .D(InstrAddr2), .clk(clock_1_out), .Q(d_ff_2_q));  // open: Qn, preset, reset
  and and_1 (and_1_out, d_ff_1_q, d_ff_2_q, clock_1_out, d_ff_3_q);
  and and_2 (and_2_out, d_ff_1_q, d_ff_2_q, clock_1_out, not_1_out);
  not not_1 (not_1_out, d_ff_3_q);
  not not_2 (not_2_out, d_ff_2_q);
  and and_3 (and_3_out, d_ff_1_q, not_2_out, clock_1_out, d_ff_3_q);
  not not_3 (not_3_out, d_ff_2_q);
  and and_4 (and_4_out, d_ff_1_q, not_3_out, clock_1_out, not_4_out);
  not not_4 (not_4_out, d_ff_3_q);
  not not_5 (not_5_out, d_ff_1_q);
  and and_5 (and_5_out, not_5_out, d_ff_2_q, clock_1_out, d_ff_3_q);
  not not_6 (not_6_out, d_ff_1_q);
  and and_6 (and_6_out, not_6_out, d_ff_2_q, clock_1_out, not_7_out);
  not not_7 (not_7_out, d_ff_3_q);
  not not_8 (not_8_out, d_ff_1_q);
  not not_9 (not_9_out, d_ff_2_q);
  and and_7 (and_7_out, not_8_out, not_9_out, clock_1_out, d_ff_3_q);
  not not_10 (not_10_out, d_ff_1_q);
  not not_11 (not_11_out, d_ff_2_q);
  not not_12 (not_12_out, d_ff_3_q);
  D_Flip_Flop #(.trigger("falling")) d_ff_3 (
    .D(InstrAddr3), .clk(clock_1_out), .Q(d_ff_3_q));  // open: Qn, preset, reset
  and and_8 (and_8_out, and_1_out, not_13_out);
  and and_9 (and_9_out, and_2_out, not_13_out);
  and and_10 (and_10_out, and_3_out, not_13_out);
  and and_11 (and_11_out, and_4_out, not_13_out);
  and and_12 (and_12_out, and_5_out, not_13_out);
  and and_13 (and_13_out, and_6_out, not_13_out);
  and and_14 (and_14_out, and_7_out, not_13_out);
  and and_15 (and_15_out, not_10_out, not_11_out, clock_1_out, not_12_out);
  and and_16 (and_16_out, and_15_out, not_13_out);
  not not_13 (not_13_out, d_ff_4_q);
  D_Flip_Flop #(.trigger("falling")) d_ff_4 (.D(Mode), .clk(clock_1_out), .Q(d_ff_4_q));  // open: Qn, preset, reset
  and and_17 (and_17_out, and_1_out, not_13_out, d_ff_13_q);
  D_Flip_Flop #(.trigger("high")) d_ff_5 (.D(and_17_out), .clk(and_8_out), .Q(d_ff_5_q));  // open: Qn, preset, reset
  and and_18 (and_18_out, and_2_out, not_13_out, d_ff_13_q);
  D_Flip_Flop #(.trigger("high")) d_ff_6 (.D(and_18_out), .clk(and_9_out), .Q(d_ff_6_q));  // open: Qn, preset, reset
  and and_19 (and_19_out, and_3_out, not_13_out, d_ff_13_q);
  D_Flip_Flop #(.trigger("high")) d_ff_7 (.D(and_19_out), .clk(and_10_out), .Q(d_ff_7_q));  // open: Qn, preset, reset
  and and_20 (and_20_out, and_4_out, not_13_out, d_ff_13_q);
  D_Flip_Flop #(.trigger("high")) d_ff_8 (.D(and_20_out), .clk(and_11_out), .Q(d_ff_8_q));  // open: Qn, preset, reset
  and and_21 (and_21_out, and_5_out, not_13_out, d_ff_13_q);
  D_Flip_Flop #(.trigger("high")) d_ff_9 (.D(and_21_out), .clk(and_12_out), .Q(d_ff_9_q));  // open: Qn, preset, reset
  and and_22 (and_22_out, and_6_out, not_13_out, d_ff_13_q);
  D_Flip_Flop #(.trigger("high")) d_ff_10 (.D(and_22_out), .clk(and_13_out), .Q(d_ff_10_q));  // open: Qn, preset, reset
  and and_23 (and_23_out, and_7_out, not_13_out, d_ff_13_q);
  D_Flip_Flop #(.trigger("high")) d_ff_11 (.D(and_23_out), .clk(and_14_out), .Q(d_ff_11_q));  // open: Qn, preset, reset
  and and_24 (and_24_out, and_15_out, not_13_out, d_ff_13_q);
  D_Flip_Flop #(.trigger("high")) d_ff_12 (.D(and_24_out), .clk(and_16_out), .Q(d_ff_12_q));  // open: Qn, preset, reset
  or or_1 (or_1_out, and_25_out, and_26_out, and_27_out, and_28_out, and_29_out, and_30_out, and_31_out, and_32_out);
  and and_25 (and_25_out, d_ff_5_q, and_1_out, d_ff_4_q);
  and and_26 (and_26_out, d_ff_6_q, and_2_out, d_ff_4_q);
  and and_27 (and_27_out, d_ff_7_q, and_3_out, d_ff_4_q);
  and and_28 (and_28_out, d_ff_8_q, and_4_out, d_ff_4_q);
  and and_29 (and_29_out, d_ff_9_q, and_5_out, d_ff_4_q);
  and and_30 (and_30_out, d_ff_10_q, and_6_out, d_ff_4_q);
  and and_31 (and_31_out, d_ff_11_q, and_7_out, d_ff_4_q);
  and and_32 (and_32_out, d_ff_12_q, and_15_out, d_ff_4_q);
  D_Flip_Flop #(.trigger("falling")) d_ff_13 (
    .D(DataInput1), .clk(clock_1_out), .Q(d_ff_13_q));  // open: Qn, preset, reset
  D_Flip_Flop #(.trigger("falling")) d_ff_14 (
    .D(DataInput2), .clk(clock_1_out), .Q(d_ff_14_q));  // open: Qn, preset, reset
  D_Flip_Flop #(.trigger("high")) d_ff_15 (.D(or_1_out), .clk(clock_1_out), .Q(Out1));  // open: Qn, preset, reset
  and and_33 (and_33_out, and_1_out, not_13_out, d_ff_14_q);
  D_Flip_Flop #(.trigger("high")) d_ff_16 (.D(and_33_out), .clk(and_8_out), .Q(d_ff_16_q));  // open: Qn, preset, reset
  and and_34 (and_34_out, and_2_out, not_13_out, d_ff_14_q);
  D_Flip_Flop #(.trigger("high")) d_ff_17 (.D(and_34_out), .clk(and_9_out), .Q(d_ff_17_q));  // open: Qn, preset, reset
  and and_35 (and_35_out, and_3_out, not_13_out, d_ff_14_q);
  D_Flip_Flop #(.trigger("high")) d_ff_18 (.D(and_35_out), .clk(and_10_out), .Q(d_ff_18_q));  // open: Qn, preset, reset
  and and_36 (and_36_out, and_4_out, not_13_out, d_ff_14_q);
  D_Flip_Flop #(.trigger("high")) d_ff_19 (.D(and_36_out), .clk(and_11_out), .Q(d_ff_19_q));  // open: Qn, preset, reset
  and and_37 (and_37_out, and_5_out, not_13_out, d_ff_14_q);
  D_Flip_Flop #(.trigger("high")) d_ff_20 (.D(and_37_out), .clk(and_12_out), .Q(d_ff_20_q));  // open: Qn, preset, reset
  and and_38 (and_38_out, and_6_out, not_13_out, d_ff_14_q);
  D_Flip_Flop #(.trigger("high")) d_ff_21 (.D(and_38_out), .clk(and_13_out), .Q(d_ff_21_q));  // open: Qn, preset, reset
  and and_39 (and_39_out, and_7_out, not_13_out, d_ff_14_q);
  D_Flip_Flop #(.trigger("high")) d_ff_22 (.D(and_39_out), .clk(and_14_out), .Q(d_ff_22_q));  // open: Qn, preset, reset
  and and_40 (and_40_out, and_15_out, not_13_out, d_ff_14_q);
  D_Flip_Flop #(.trigger("high")) d_ff_23 (.D(and_40_out), .clk(and_16_out), .Q(d_ff_23_q));  // open: Qn, preset, reset
  D_Flip_Flop #(.trigger("falling")) d_ff_24 (
    .D(DataInput3), .clk(clock_1_out), .Q(d_ff_24_q));  // open: Qn, preset, reset
  D_Flip_Flop #(.trigger("high")) d_ff_25 (.D(or_2_out), .clk(clock_1_out), .Q(Out2));  // open: Qn, preset, reset
  or or_2 (or_2_out, and_41_out, and_42_out, and_43_out, and_44_out, and_45_out, and_46_out, and_47_out, and_48_out);
  and and_41 (and_41_out, d_ff_16_q, and_1_out, d_ff_4_q);
  and and_42 (and_42_out, d_ff_17_q, and_2_out, d_ff_4_q);
  and and_43 (and_43_out, d_ff_18_q, and_3_out, d_ff_4_q);
  and and_44 (and_44_out, d_ff_19_q, and_4_out, d_ff_4_q);
  and and_45 (and_45_out, d_ff_20_q, and_5_out, d_ff_4_q);
  and and_46 (and_46_out, d_ff_21_q, and_6_out, d_ff_4_q);
  and and_47 (and_47_out, d_ff_22_q, and_7_out, d_ff_4_q);
  and and_48 (and_48_out, d_ff_23_q, and_15_out, d_ff_4_q);
  D_Flip_Flop #(.trigger("falling")) d_ff_26 (
    .D(DataInput4), .clk(clock_1_out), .Q(d_ff_26_q));  // open: Qn, preset, reset
  D_Flip_Flop #(.trigger("high")) d_ff_27 (.D(or_3_out), .clk(clock_1_out), .Q(Out3));  // open: Qn, preset, reset
  D_Flip_Flop #(.trigger("high")) d_ff_28 (.D(or_4_out), .clk(clock_1_out), .Q(Out4));  // open: Qn, preset, reset
  and and_49 (and_49_out, and_1_out, not_13_out, d_ff_24_q);
  and and_50 (and_50_out, and_2_out, not_13_out, d_ff_24_q);
  and and_51 (and_51_out, and_3_out, not_13_out, d_ff_24_q);
  and and_52 (and_52_out, and_4_out, not_13_out, d_ff_24_q);
  and and_53 (and_53_out, and_5_out, not_13_out, d_ff_24_q);
  and and_54 (and_54_out, and_6_out, not_13_out, d_ff_24_q);
  and and_55 (and_55_out, and_7_out, not_13_out, d_ff_24_q);
  and and_56 (and_56_out, and_15_out, not_13_out, d_ff_24_q);
  or or_3 (or_3_out, and_57_out, and_58_out, and_59_out, and_60_out, and_61_out, and_62_out, and_63_out, and_64_out);
  and and_57 (and_57_out, d_ff_29_q, and_1_out, d_ff_4_q);
  D_Flip_Flop #(.trigger("high")) d_ff_29 (.D(and_49_out), .clk(and_8_out), .Q(d_ff_29_q));  // open: Qn, preset, reset
  and and_58 (and_58_out, d_ff_30_q, and_2_out, d_ff_4_q);
  D_Flip_Flop #(.trigger("high")) d_ff_30 (.D(and_50_out), .clk(and_9_out), .Q(d_ff_30_q));  // open: Qn, preset, reset
  and and_59 (and_59_out, d_ff_31_q, and_3_out, d_ff_4_q);
  D_Flip_Flop #(.trigger("high")) d_ff_31 (.D(and_51_out), .clk(and_10_out), .Q(d_ff_31_q));  // open: Qn, preset, reset
  and and_60 (and_60_out, d_ff_32_q, and_4_out, d_ff_4_q);
  D_Flip_Flop #(.trigger("high")) d_ff_32 (.D(and_52_out), .clk(and_11_out), .Q(d_ff_32_q));  // open: Qn, preset, reset
  and and_61 (and_61_out, d_ff_33_q, and_5_out, d_ff_4_q);
  D_Flip_Flop #(.trigger("high")) d_ff_33 (.D(and_53_out), .clk(and_12_out), .Q(d_ff_33_q));  // open: Qn, preset, reset
  and and_62 (and_62_out, d_ff_34_q, and_6_out, d_ff_4_q);
  D_Flip_Flop #(.trigger("high")) d_ff_34 (.D(and_54_out), .clk(and_13_out), .Q(d_ff_34_q));  // open: Qn, preset, reset
  and and_63 (and_63_out, d_ff_35_q, and_7_out, d_ff_4_q);
  D_Flip_Flop #(.trigger("high")) d_ff_35 (.D(and_55_out), .clk(and_14_out), .Q(d_ff_35_q));  // open: Qn, preset, reset
  and and_64 (and_64_out, d_ff_36_q, and_15_out, d_ff_4_q);
  D_Flip_Flop #(.trigger("high")) d_ff_36 (.D(and_56_out), .clk(and_16_out), .Q(d_ff_36_q));  // open: Qn, preset, reset
  and and_65 (and_65_out, and_1_out, not_13_out, d_ff_26_q);
  D_Flip_Flop #(.trigger("high")) d_ff_37 (.D(and_65_out), .clk(and_8_out), .Q(d_ff_37_q));  // open: Qn, preset, reset
  and and_66 (and_66_out, and_2_out, not_13_out, d_ff_26_q);
  D_Flip_Flop #(.trigger("high")) d_ff_38 (.D(and_66_out), .clk(and_9_out), .Q(d_ff_38_q));  // open: Qn, preset, reset
  and and_67 (and_67_out, and_3_out, not_13_out, d_ff_26_q);
  D_Flip_Flop #(.trigger("high")) d_ff_39 (.D(and_67_out), .clk(and_10_out), .Q(d_ff_39_q));  // open: Qn, preset, reset
  and and_68 (and_68_out, and_4_out, not_13_out, d_ff_26_q);
  D_Flip_Flop #(.trigger("high")) d_ff_40 (.D(and_68_out), .clk(and_11_out), .Q(d_ff_40_q));  // open: Qn, preset, reset
  and and_69 (and_69_out, and_5_out, not_13_out, d_ff_26_q);
  D_Flip_Flop #(.trigger("high")) d_ff_41 (.D(and_69_out), .clk(and_12_out), .Q(d_ff_41_q));  // open: Qn, preset, reset
  and and_70 (and_70_out, and_6_out, not_13_out, d_ff_26_q);
  D_Flip_Flop #(.trigger("high")) d_ff_42 (.D(and_70_out), .clk(and_13_out), .Q(d_ff_42_q));  // open: Qn, preset, reset
  and and_71 (and_71_out, and_7_out, not_13_out, d_ff_26_q);
  D_Flip_Flop #(.trigger("high")) d_ff_43 (.D(and_71_out), .clk(and_14_out), .Q(d_ff_43_q));  // open: Qn, preset, reset
  and and_72 (and_72_out, and_15_out, not_13_out, d_ff_26_q);
  D_Flip_Flop #(.trigger("high")) d_ff_44 (.D(and_72_out), .clk(and_16_out), .Q(d_ff_44_q));  // open: Qn, preset, reset
  or or_4 (or_4_out, and_73_out, and_74_out, and_75_out, and_76_out, and_77_out, and_78_out, and_79_out, and_80_out);
  and and_73 (and_73_out, d_ff_37_q, and_1_out, d_ff_4_q);
  and and_74 (and_74_out, d_ff_38_q, and_2_out, d_ff_4_q);
  and and_75 (and_75_out, d_ff_39_q, and_3_out, d_ff_4_q);
  and and_76 (and_76_out, d_ff_40_q, and_4_out, d_ff_4_q);
  and and_77 (and_77_out, d_ff_41_q, and_5_out, d_ff_4_q);
  and and_78 (and_78_out, d_ff_42_q, and_6_out, d_ff_4_q);
  and and_79 (and_79_out, d_ff_43_q, and_7_out, d_ff_4_q);
  and and_80 (and_80_out, d_ff_44_q, and_15_out, d_ff_4_q);

  // Notes on the sheet:
  //   3-bit address input pins
  //   Mode input pin
  //   4-bit data input pins
endmodule

module PC (
);

  wire undriven;

  D_Flip_Flop d_ff_1 (.D(undriven));  // open: clk, Q, Qn, preset, reset
  D_Flip_Flop d_ff_2 ();  // open: D, clk, Q, Qn, preset, reset
  D_Flip_Flop d_ff_3 ();  // open: D, clk, Q, Qn, preset, reset
  D_Flip_Flop d_ff_4 ();  // open: D, clk, Q, Qn, preset, reset
  D_Flip_Flop d_ff_5 ();  // open: D, clk, Q, Qn, preset, reset
  D_Flip_Flop d_ff_6 ();  // open: D, clk, Q, Qn, preset, reset
  D_Flip_Flop d_ff_7 ();  // open: D, clk, Q, Qn, preset, reset
  D_Flip_Flop d_ff_8 ();  // open: D, clk, Q, Qn, preset, reset
endmodule

module dataRAM (
  input  InstrAddr1,
  input  InstrAddr2,
  input  InstrAddr3,
  input  Mode,
  input  DataInput1,
  input  DataInput2,
  input  DataInput3,
  input  DataInput4,
  output IrOut1,
  output IrOut2,
  output IrOut3,
  output IrOut4
);

  wire and_1_out, and_2_out, and_3_out, and_4_out, and_5_out, and_6_out, and_7_out, and_8_out, and_9_out,
       and_10_out, and_11_out, and_12_out, and_13_out, and_14_out, and_15_out, and_16_out, and_17_out,
       and_18_out, and_19_out, and_20_out, and_21_out, and_22_out, and_23_out, and_24_out, and_25_out,
       and_26_out, and_27_out, and_28_out, and_29_out, and_30_out, and_31_out, and_32_out, and_33_out,
       and_34_out, and_35_out, and_36_out, and_37_out, and_38_out, and_39_out, and_40_out, and_41_out,
       and_42_out, and_43_out, and_44_out, and_45_out, and_46_out, and_47_out, and_48_out, and_49_out,
       and_50_out, and_51_out, and_52_out, and_53_out, and_54_out, and_55_out, and_56_out, and_57_out,
       and_58_out, and_59_out, and_60_out, and_61_out, and_62_out, and_63_out, and_64_out, and_65_out,
       and_66_out, and_67_out, and_68_out, and_69_out, and_70_out, and_71_out, and_72_out, and_73_out,
       and_74_out, and_75_out, and_76_out, and_77_out, and_78_out, and_79_out, and_80_out, clock_1_out,
       d_ff_1_q, d_ff_2_q, d_ff_3_q, d_ff_4_q, d_ff_5_q, d_ff_6_q, d_ff_7_q, d_ff_8_q, d_ff_9_q, d_ff_10_q,
       d_ff_11_q, d_ff_12_q, d_ff_13_q, d_ff_14_q, d_ff_16_q, d_ff_17_q, d_ff_18_q, d_ff_19_q, d_ff_20_q,
       d_ff_21_q, d_ff_22_q, d_ff_23_q, d_ff_24_q, d_ff_26_q, d_ff_29_q, d_ff_30_q, d_ff_31_q, d_ff_32_q,
       d_ff_33_q, d_ff_34_q, d_ff_35_q, d_ff_36_q, d_ff_37_q, d_ff_38_q, d_ff_39_q, d_ff_40_q, d_ff_41_q,
       d_ff_42_q, d_ff_43_q, d_ff_44_q, not_1_out, not_2_out, not_3_out, not_4_out, not_5_out, not_6_out,
       not_7_out, not_8_out, not_9_out, not_10_out, not_11_out, not_12_out, not_13_out, or_1_out, or_2_out,
       or_3_out, or_4_out;

  D_Flip_Flop #(.trigger("falling")) d_ff_1 (
    .D(InstrAddr1), .clk(clock_1_out), .Q(d_ff_1_q));  // open: Qn, preset, reset
  Clock clock_1 (.out(clock_1_out));
  D_Flip_Flop #(.trigger("falling")) d_ff_2 (
    .D(InstrAddr2), .clk(clock_1_out), .Q(d_ff_2_q));  // open: Qn, preset, reset
  and and_1 (and_1_out, d_ff_1_q, d_ff_2_q, clock_1_out, d_ff_3_q);
  and and_2 (and_2_out, d_ff_1_q, d_ff_2_q, clock_1_out, not_1_out);
  not not_1 (not_1_out, d_ff_3_q);
  not not_2 (not_2_out, d_ff_2_q);
  and and_3 (and_3_out, d_ff_1_q, not_2_out, clock_1_out, d_ff_3_q);
  not not_3 (not_3_out, d_ff_2_q);
  and and_4 (and_4_out, d_ff_1_q, not_3_out, clock_1_out, not_4_out);
  not not_4 (not_4_out, d_ff_3_q);
  not not_5 (not_5_out, d_ff_1_q);
  and and_5 (and_5_out, not_5_out, d_ff_2_q, clock_1_out, d_ff_3_q);
  not not_6 (not_6_out, d_ff_1_q);
  and and_6 (and_6_out, not_6_out, d_ff_2_q, clock_1_out, not_7_out);
  not not_7 (not_7_out, d_ff_3_q);
  not not_8 (not_8_out, d_ff_1_q);
  not not_9 (not_9_out, d_ff_2_q);
  and and_7 (and_7_out, not_8_out, not_9_out, clock_1_out, d_ff_3_q);
  not not_10 (not_10_out, d_ff_1_q);
  not not_11 (not_11_out, d_ff_2_q);
  not not_12 (not_12_out, d_ff_3_q);
  D_Flip_Flop #(.trigger("falling")) d_ff_3 (
    .D(InstrAddr3), .clk(clock_1_out), .Q(d_ff_3_q));  // open: Qn, preset, reset
  and and_8 (and_8_out, and_1_out, not_13_out);
  and and_9 (and_9_out, and_2_out, not_13_out);
  and and_10 (and_10_out, and_3_out, not_13_out);
  and and_11 (and_11_out, and_4_out, not_13_out);
  and and_12 (and_12_out, and_5_out, not_13_out);
  and and_13 (and_13_out, and_6_out, not_13_out);
  and and_14 (and_14_out, and_7_out, not_13_out);
  and and_15 (and_15_out, not_10_out, not_11_out, clock_1_out, not_12_out);
  and and_16 (and_16_out, and_15_out, not_13_out);
  not not_13 (not_13_out, d_ff_4_q);
  D_Flip_Flop #(.trigger("falling")) d_ff_4 (.D(Mode), .clk(clock_1_out), .Q(d_ff_4_q));  // open: Qn, preset, reset
  and and_17 (and_17_out, and_1_out, not_13_out, d_ff_13_q);
  D_Flip_Flop #(.trigger("high")) d_ff_5 (.D(and_17_out), .clk(and_8_out), .Q(d_ff_5_q));  // open: Qn, preset, reset
  and and_18 (and_18_out, and_2_out, not_13_out, d_ff_13_q);
  D_Flip_Flop #(.trigger("high")) d_ff_6 (.D(and_18_out), .clk(and_9_out), .Q(d_ff_6_q));  // open: Qn, preset, reset
  and and_19 (and_19_out, and_3_out, not_13_out, d_ff_13_q);
  D_Flip_Flop #(.trigger("high")) d_ff_7 (.D(and_19_out), .clk(and_10_out), .Q(d_ff_7_q));  // open: Qn, preset, reset
  and and_20 (and_20_out, and_4_out, not_13_out, d_ff_13_q);
  D_Flip_Flop #(.trigger("high")) d_ff_8 (.D(and_20_out), .clk(and_11_out), .Q(d_ff_8_q));  // open: Qn, preset, reset
  and and_21 (and_21_out, and_5_out, not_13_out, d_ff_13_q);
  D_Flip_Flop #(.trigger("high")) d_ff_9 (.D(and_21_out), .clk(and_12_out), .Q(d_ff_9_q));  // open: Qn, preset, reset
  and and_22 (and_22_out, and_6_out, not_13_out, d_ff_13_q);
  D_Flip_Flop #(.trigger("high")) d_ff_10 (.D(and_22_out), .clk(and_13_out), .Q(d_ff_10_q));  // open: Qn, preset, reset
  and and_23 (and_23_out, and_7_out, not_13_out, d_ff_13_q);
  D_Flip_Flop #(.trigger("high")) d_ff_11 (.D(and_23_out), .clk(and_14_out), .Q(d_ff_11_q));  // open: Qn, preset, reset
  and and_24 (and_24_out, and_15_out, not_13_out, d_ff_13_q);
  D_Flip_Flop #(.trigger("high")) d_ff_12 (.D(and_24_out), .clk(and_16_out), .Q(d_ff_12_q));  // open: Qn, preset, reset
  or or_1 (or_1_out, and_25_out, and_26_out, and_27_out, and_28_out, and_29_out, and_30_out, and_31_out, and_32_out);
  and and_25 (and_25_out, d_ff_5_q, and_1_out, d_ff_4_q);
  and and_26 (and_26_out, d_ff_6_q, and_2_out, d_ff_4_q);
  and and_27 (and_27_out, d_ff_7_q, and_3_out, d_ff_4_q);
  and and_28 (and_28_out, d_ff_8_q, and_4_out, d_ff_4_q);
  and and_29 (and_29_out, d_ff_9_q, and_5_out, d_ff_4_q);
  and and_30 (and_30_out, d_ff_10_q, and_6_out, d_ff_4_q);
  and and_31 (and_31_out, d_ff_11_q, and_7_out, d_ff_4_q);
  and and_32 (and_32_out, d_ff_12_q, and_15_out, d_ff_4_q);
  D_Flip_Flop #(.trigger("falling")) d_ff_13 (
    .D(DataInput1), .clk(clock_1_out), .Q(d_ff_13_q));  // open: Qn, preset, reset
  D_Flip_Flop #(.trigger("falling")) d_ff_14 (
    .D(DataInput2), .clk(clock_1_out), .Q(d_ff_14_q));  // open: Qn, preset, reset
  D_Flip_Flop #(.trigger("high")) d_ff_15 (.D(or_1_out), .clk(clock_1_out), .Q(IrOut1));  // open: Qn, preset, reset
  and and_33 (and_33_out, and_1_out, not_13_out, d_ff_14_q);
  D_Flip_Flop #(.trigger("high")) d_ff_16 (.D(and_33_out), .clk(and_8_out), .Q(d_ff_16_q));  // open: Qn, preset, reset
  and and_34 (and_34_out, and_2_out, not_13_out, d_ff_14_q);
  D_Flip_Flop #(.trigger("high")) d_ff_17 (.D(and_34_out), .clk(and_9_out), .Q(d_ff_17_q));  // open: Qn, preset, reset
  and and_35 (and_35_out, and_3_out, not_13_out, d_ff_14_q);
  D_Flip_Flop #(.trigger("high")) d_ff_18 (.D(and_35_out), .clk(and_10_out), .Q(d_ff_18_q));  // open: Qn, preset, reset
  and and_36 (and_36_out, and_4_out, not_13_out, d_ff_14_q);
  D_Flip_Flop #(.trigger("high")) d_ff_19 (.D(and_36_out), .clk(and_11_out), .Q(d_ff_19_q));  // open: Qn, preset, reset
  and and_37 (and_37_out, and_5_out, not_13_out, d_ff_14_q);
  D_Flip_Flop #(.trigger("high")) d_ff_20 (.D(and_37_out), .clk(and_12_out), .Q(d_ff_20_q));  // open: Qn, preset, reset
  and and_38 (and_38_out, and_6_out, not_13_out, d_ff_14_q);
  D_Flip_Flop #(.trigger("high")) d_ff_21 (.D(and_38_out), .clk(and_13_out), .Q(d_ff_21_q));  // open: Qn, preset, reset
  and and_39 (and_39_out, and_7_out, not_13_out, d_ff_14_q);
  D_Flip_Flop #(.trigger("high")) d_ff_22 (.D(and_39_out), .clk(and_14_out), .Q(d_ff_22_q));  // open: Qn, preset, reset
  and and_40 (and_40_out, and_15_out, not_13_out, d_ff_14_q);
  D_Flip_Flop #(.trigger("high")) d_ff_23 (.D(and_40_out), .clk(and_16_out), .Q(d_ff_23_q));  // open: Qn, preset, reset
  D_Flip_Flop #(.trigger("falling")) d_ff_24 (
    .D(DataInput3), .clk(clock_1_out), .Q(d_ff_24_q));  // open: Qn, preset, reset
  D_Flip_Flop #(.trigger("high")) d_ff_25 (.D(or_2_out), .clk(clock_1_out), .Q(IrOut2));  // open: Qn, preset, reset
  or or_2 (or_2_out, and_41_out, and_42_out, and_43_out, and_44_out, and_45_out, and_46_out, and_47_out, and_48_out);
  and and_41 (and_41_out, d_ff_16_q, and_1_out, d_ff_4_q);
  and and_42 (and_42_out, d_ff_17_q, and_2_out, d_ff_4_q);
  and and_43 (and_43_out, d_ff_18_q, and_3_out, d_ff_4_q);
  and and_44 (and_44_out, d_ff_19_q, and_4_out, d_ff_4_q);
  and and_45 (and_45_out, d_ff_20_q, and_5_out, d_ff_4_q);
  and and_46 (and_46_out, d_ff_21_q, and_6_out, d_ff_4_q);
  and and_47 (and_47_out, d_ff_22_q, and_7_out, d_ff_4_q);
  and and_48 (and_48_out, d_ff_23_q, and_15_out, d_ff_4_q);
  D_Flip_Flop #(.trigger("falling")) d_ff_26 (
    .D(DataInput4), .clk(clock_1_out), .Q(d_ff_26_q));  // open: Qn, preset, reset
  D_Flip_Flop #(.trigger("high")) d_ff_27 (.D(or_3_out), .clk(clock_1_out), .Q(IrOut3));  // open: Qn, preset, reset
  D_Flip_Flop #(.trigger("high")) d_ff_28 (.D(or_4_out), .clk(clock_1_out), .Q(IrOut4));  // open: Qn, preset, reset
  and and_49 (and_49_out, and_1_out, not_13_out, d_ff_24_q);
  and and_50 (and_50_out, and_2_out, not_13_out, d_ff_24_q);
  and and_51 (and_51_out, and_3_out, not_13_out, d_ff_24_q);
  and and_52 (and_52_out, and_4_out, not_13_out, d_ff_24_q);
  and and_53 (and_53_out, and_5_out, not_13_out, d_ff_24_q);
  and and_54 (and_54_out, and_6_out, not_13_out, d_ff_24_q);
  and and_55 (and_55_out, and_7_out, not_13_out, d_ff_24_q);
  and and_56 (and_56_out, and_15_out, not_13_out, d_ff_24_q);
  or or_3 (or_3_out, and_57_out, and_58_out, and_59_out, and_60_out, and_61_out, and_62_out, and_63_out, and_64_out);
  and and_57 (and_57_out, d_ff_29_q, and_1_out, d_ff_4_q);
  D_Flip_Flop #(.trigger("high")) d_ff_29 (.D(and_49_out), .clk(and_8_out), .Q(d_ff_29_q));  // open: Qn, preset, reset
  and and_58 (and_58_out, d_ff_30_q, and_2_out, d_ff_4_q);
  D_Flip_Flop #(.trigger("high")) d_ff_30 (.D(and_50_out), .clk(and_9_out), .Q(d_ff_30_q));  // open: Qn, preset, reset
  and and_59 (and_59_out, d_ff_31_q, and_3_out, d_ff_4_q);
  D_Flip_Flop #(.trigger("high")) d_ff_31 (.D(and_51_out), .clk(and_10_out), .Q(d_ff_31_q));  // open: Qn, preset, reset
  and and_60 (and_60_out, d_ff_32_q, and_4_out, d_ff_4_q);
  D_Flip_Flop #(.trigger("high")) d_ff_32 (.D(and_52_out), .clk(and_11_out), .Q(d_ff_32_q));  // open: Qn, preset, reset
  and and_61 (and_61_out, d_ff_33_q, and_5_out, d_ff_4_q);
  D_Flip_Flop #(.trigger("high")) d_ff_33 (.D(and_53_out), .clk(and_12_out), .Q(d_ff_33_q));  // open: Qn, preset, reset
  and and_62 (and_62_out, d_ff_34_q, and_6_out, d_ff_4_q);
  D_Flip_Flop #(.trigger("high")) d_ff_34 (.D(and_54_out), .clk(and_13_out), .Q(d_ff_34_q));  // open: Qn, preset, reset
  and and_63 (and_63_out, d_ff_35_q, and_7_out, d_ff_4_q);
  D_Flip_Flop #(.trigger("high")) d_ff_35 (.D(and_55_out), .clk(and_14_out), .Q(d_ff_35_q));  // open: Qn, preset, reset
  and and_64 (and_64_out, d_ff_36_q, and_15_out, d_ff_4_q);
  D_Flip_Flop #(.trigger("high")) d_ff_36 (.D(and_56_out), .clk(and_16_out), .Q(d_ff_36_q));  // open: Qn, preset, reset
  and and_65 (and_65_out, and_1_out, not_13_out, d_ff_26_q);
  D_Flip_Flop #(.trigger("high")) d_ff_37 (.D(and_65_out), .clk(and_8_out), .Q(d_ff_37_q));  // open: Qn, preset, reset
  and and_66 (and_66_out, and_2_out, not_13_out, d_ff_26_q);
  D_Flip_Flop #(.trigger("high")) d_ff_38 (.D(and_66_out), .clk(and_9_out), .Q(d_ff_38_q));  // open: Qn, preset, reset
  and and_67 (and_67_out, and_3_out, not_13_out, d_ff_26_q);
  D_Flip_Flop #(.trigger("high")) d_ff_39 (.D(and_67_out), .clk(and_10_out), .Q(d_ff_39_q));  // open: Qn, preset, reset
  and and_68 (and_68_out, and_4_out, not_13_out, d_ff_26_q);
  D_Flip_Flop #(.trigger("high")) d_ff_40 (.D(and_68_out), .clk(and_11_out), .Q(d_ff_40_q));  // open: Qn, preset, reset
  and and_69 (and_69_out, and_5_out, not_13_out, d_ff_26_q);
  D_Flip_Flop #(.trigger("high")) d_ff_41 (.D(and_69_out), .clk(and_12_out), .Q(d_ff_41_q));  // open: Qn, preset, reset
  and and_70 (and_70_out, and_6_out, not_13_out, d_ff_26_q);
  D_Flip_Flop #(.trigger("high")) d_ff_42 (.D(and_70_out), .clk(and_13_out), .Q(d_ff_42_q));  // open: Qn, preset, reset
  and and_71 (and_71_out, and_7_out, not_13_out, d_ff_26_q);
  D_Flip_Flop #(.trigger("high")) d_ff_43 (.D(and_71_out), .clk(and_14_out), .Q(d_ff_43_q));  // open: Qn, preset, reset
  and and_72 (and_72_out, and_15_out, not_13_out, d_ff_26_q);
  D_Flip_Flop #(.trigger("high")) d_ff_44 (.D(and_72_out), .clk(and_16_out), .Q(d_ff_44_q));  // open: Qn, preset, reset
  or or_4 (or_4_out, and_73_out, and_74_out, and_75_out, and_76_out, and_77_out, and_78_out, and_79_out, and_80_out);
  and and_73 (and_73_out, d_ff_37_q, and_1_out, d_ff_4_q);
  and and_74 (and_74_out, d_ff_38_q, and_2_out, d_ff_4_q);
  and and_75 (and_75_out, d_ff_39_q, and_3_out, d_ff_4_q);
  and and_76 (and_76_out, d_ff_40_q, and_4_out, d_ff_4_q);
  and and_77 (and_77_out, d_ff_41_q, and_5_out, d_ff_4_q);
  and and_78 (and_78_out, d_ff_42_q, and_6_out, d_ff_4_q);
  and and_79 (and_79_out, d_ff_43_q, and_7_out, d_ff_4_q);
  and and_80 (and_80_out, d_ff_44_q, and_15_out, d_ff_4_q);

  // Notes on the sheet:
  //   3-bit address input pins
  //   Mode input pin
  //   4-bit data input pins
endmodule

module MyALU (
  input  L1,
  input  L2,
  input  L3,
  input  L4,
  input  R1,
  input  R2,
  input  R3,
  input  R4,
  input  cmd,
  input  in_10,
  output out_11,
  output out_12,
  output out_13,
  output out1,
  output out2,
  output out3,
  output out4
);

  wire and_1_out, and_2_out, and_3_out, and_4_out, and_5_out, and_6_out, and_7_out, and_8_out, and_9_out,
       and_10_out, and_11_out, and_12_out, and_13_out, and_14_out, and_15_out, and_16_out, and_17_out,
       and_18_out, and_19_out, and_20_out, and_21_out, and_22_out, and_23_out, and_24_out, and_25_out,
       and_26_out, and_27_out, and_28_out, clock_1_out, d_ff_2_q, d_ff_5_q, d_ff_6_q, d_ff_8_q, d_ff_9_q,
       d_ff_10_q, d_ff_11_q, d_ff_12_q, d_ff_13_q, d_ff_14_q, not_1_out, not_2_out, not_3_out, not_4_out,
       not_5_out, not_6_out, not_7_out, not_8_out, not_9_out, not_10_out, not_11_out, not_12_out, not_13_out,
       not_14_out, not_15_out, or_1_out, or_2_out, or_3_out, or_4_out, or_5_out, or_6_out, or_7_out,
       or_8_out, or_9_out, or_10_out, or_11_out, or_12_out, or_13_out, or_14_out, xor_1_out, xor_2_out,
       xor_3_out, xor_4_out;

  Clock clock_1 (.out(clock_1_out));
  not not_1 (not_1_out, cmd);
  and and_1 (and_1_out, or_4_out, and_17_out);
  and and_2 (and_2_out, or_4_out, d_ff_5_q);
  or or_1 (or_1_out, and_1_out, and_2_out, and_3_out);
  and and_3 (and_3_out, and_17_out, d_ff_5_q);
  not not_2 (not_2_out, or_1_out);
  and and_4 (and_4_out, not_2_out, or_2_out);
  not not_3 (not_3_out, d_ff_5_q);
  and and_5 (and_5_out, or_3_out, not_3_out, not_4_out, not_1_out);
  not not_4 (not_4_out, and_17_out);
  or or_2 (or_2_out, or_4_out, and_17_out, d_ff_5_q);
  and and_6 (and_6_out, or_4_out, and_17_out, d_ff_5_q);
  or or_3 (or_3_out, and_4_out, and_6_out);
  and and_7 (and_7_out, or_7_out, and_20_out);
  and and_8 (and_8_out, or_7_out, d_ff_6_q);
  or or_4 (or_4_out, and_7_out, and_8_out, and_9_out);
  D_Flip_Flop d_ff_1 (.D(or_3_out), .clk(clock_1_out), .Q(out1));  // open: Qn, preset, reset
  D_Flip_Flop d_ff_2 (.D(cmd), .clk(clock_1_out), .Q(d_ff_2_q));  // open: Qn, preset, reset
  and and_9 (and_9_out, and_20_out, d_ff_6_q);
  not not_5 (not_5_out, or_4_out);
  D_Flip_Flop d_ff_3 (.D(or_6_out), .clk(clock_1_out), .Q(out2));  // open: Qn, preset, reset
  or or_5 (or_5_out, or_7_out, and_20_out, d_ff_6_q);
  and and_10 (and_10_out, not_5_out, or_5_out);
  or or_6 (or_6_out, and_10_out, and_11_out);
  D_Flip_Flop d_ff_4 (.D(or_9_out), .clk(clock_1_out), .Q(out3));  // open: Qn, preset, reset
  D_Flip_Flop d_ff_5 (.D(L1), .clk(clock_1_out), .Q(d_ff_5_q));  // open: Qn, preset, reset
  and and_11 (and_11_out, or_7_out, and_20_out, d_ff_6_q);
  D_Flip_Flop d_ff_6 (.D(L2), .clk(clock_1_out), .Q(d_ff_6_q));  // open: Qn, preset, reset
  and and_12 (and_12_out, and_23_out, and_22_out);
  D_Flip_Flop d_ff_7 (.D(and_25_out), .clk(clock_1_out), .Q(out4));  // open: Qn, preset, reset
  and and_13 (and_13_out, and_23_out, d_ff_8_q);
  and and_14 (and_14_out, and_22_out, d_ff_8_q);
  or or_7 (or_7_out, and_12_out, and_13_out, and_14_out);
  not not_6 (not_6_out, or_7_out);
  D_Flip_Flop d_ff_8 (.D(L3), .clk(clock_1_out), .Q(d_ff_8_q));  // open: Qn, preset, reset
  or or_8 (or_8_out, and_23_out, and_22_out, d_ff_8_q);
  and and_15 (and_15_out, not_6_out, or_8_out);
  D_Flip_Flop d_ff_9 (.D(L4), .clk(clock_1_out), .Q(d_ff_9_q));  // open: Qn, preset, reset
  and and_16 (and_16_out, and_19_out, xor_1_out);
  not not_7 (not_7_out, and_16_out);
  and and_17 (and_17_out, not_7_out, or_10_out);
  and and_18 (and_18_out, and_23_out, and_22_out, d_ff_8_q);
  or or_9 (or_9_out, and_15_out, and_18_out);
  or or_10 (or_10_out, and_19_out, xor_1_out);
  D_Flip_Flop d_ff_10 (.D(R1), .clk(clock_1_out), .Q(d_ff_10_q));  // open: Qn, preset, reset
  xor xor_1 (xor_1_out, d_ff_2_q, d_ff_10_q);
  and and_19 (and_19_out, and_21_out, xor_2_out);
  not not_8 (not_8_out, and_19_out);
  and and_20 (and_20_out, not_8_out, or_11_out);
  D_Flip_Flop d_ff_11 (.D(R2), .clk(clock_1_out), .Q(d_ff_11_q));  // open: Qn, preset, reset
  xor xor_2 (xor_2_out, d_ff_2_q, d_ff_11_q);
  or or_11 (or_11_out, and_21_out, xor_2_out);
  D_Flip_Flop d_ff_12 (.D(R3), .clk(clock_1_out), .Q(d_ff_12_q));  // open: Qn, preset, reset
  and and_21 (and_21_out, and_24_out, xor_3_out);
  or or_12 (or_12_out, and_24_out, xor_3_out);
  not not_9 (not_9_out, and_21_out);
  and and_22 (and_22_out, not_9_out, or_12_out);
  D_Flip_Flop d_ff_13 (.D(R4), .clk(clock_1_out), .Q(d_ff_13_q));  // open: Qn, preset, reset
  xor xor_3 (xor_3_out, d_ff_2_q, d_ff_12_q);
  and and_23 (and_23_out, d_ff_9_q, and_27_out);
  xor xor_4 (xor_4_out, d_ff_2_q, d_ff_13_q);
  and and_24 (and_24_out, and_26_out, xor_4_out);
  not not_10 (not_10_out, and_24_out);
  or or_13 (or_13_out, d_ff_9_q, and_27_out);
  not not_11 (not_11_out, and_23_out);
  and and_25 (and_25_out, not_11_out, or_13_out);
  and and_26 (and_26_out, d_ff_2_q, d_ff_14_q);
  or or_14 (or_14_out, and_26_out, xor_4_out);
  and and_27 (and_27_out, not_10_out, or_14_out);
  not not_12 (not_12_out, or_3_out);
  not not_13 (not_13_out, or_6_out);
  not not_14 (not_14_out, or_9_out);
  not not_15 (not_15_out, and_25_out);
  and and_28 (and_28_out, not_12_out, not_13_out, not_14_out, not_15_out);
  D_Flip_Flop d_ff_14 (.D(in_10), .clk(clock_1_out), .Q(d_ff_14_q));  // open: Qn, preset, reset
  D_Flip_Flop d_ff_15 (.D(or_3_out), .clk(clock_1_out), .Q(out_11));  // open: Qn, preset, reset
  D_Flip_Flop d_ff_16 (.D(and_28_out), .clk(clock_1_out), .Q(out_12));  // open: Qn, preset, reset
  D_Flip_Flop d_ff_17 (.D(and_5_out), .clk(clock_1_out), .Q(out_13));  // open: Qn, preset, reset

  // Notes on the sheet:
  //   Leticia Huang 261068858
  //   Add/Sub command
  //   A-out output
  //   L input
  //   R input
  //   Add 1 to 2's comp, plz turn to 1 before testing
  //   Status output
endmodule
